# Fritzing sketch speeduino pro NA6 (saved by Fritzing 0.9.3b)
circuit board: 10cm x 10cm
breadboards: 1

parts:
  Arduino_Mega_2560 = Arduino Mega 2560 (Rev3) [part_number="Arduino Mega 2560"]
  D15 = Schottky Diode [part_number=1N5818 package="300 mil [THT]"]
  U2 = V18ZA2P [part_number=ERZV14D220 package=v18za2p]
  IC7 = LQFP-48 [chip_label=LQFP-48 part_number=MC33814 package=LQFP]
  IC2 = SO08 [chip_label=IC part_number=TC4424AVOA package=SO]
  IC1 = SO08 [chip_label=IC part_number=TC4424AVOA package=SO]
  R35 = Resistor [tolerance=±5% resistance=100k part_number=RC0805FR-07100KL package="0805 [SMD]"]
  R37 = Resistor [tolerance=±5% resistance=100k part_number=RC0805FR-07100KL package="0805 [SMD]"]
  IC4 = SO08 [chip_label=SO08 part_number=VNLD5090-E package=SO]
  R17 = Resistor [tolerance=±5% resistance=100k package="0805 [SMD]"]
  R59 = Resistor [tolerance=±1% resistance=1k part_number=RC0805FR-071KL package="0805 [SMD]"]
  R60 = Resistor [tolerance=±1% resistance=1k part_number=RC0805FR-071KL package="0805 [SMD]"]
  R61 = Resistor [tolerance=±5% resistance=100k package="0805 [SMD]"]
  R12 = Resistor [tolerance=±5% resistance=2.4k power=0.25W package="0805 [SMD]"]
  R9 = Resistor [tolerance=±5% resistance=2.4k package="0805 [SMD]"]
  LED2 = smd LED [color="Red (633nm)" part_number="LH R974-LP-1" package="0805 [SMD]"]
  C14 = Tantalum Capacitor [capacitance=47µF voltage=10V part_number=TAJB476K006RNJ package="B 3528 [SMD, tantalum]"]
  C13 = Ceramic Capacitor [capacitance=0.1µF voltage=50V part_number=C1206C104K5RAC7867 package="1206 [SMD, multilayer]"]
  C24 = Ceramic Capacitor [capacitance=0.1µF voltage=50V part_number=C1206C104K5RAC7867 package="1206 [SMD, multilayer]"]
  C25 = Tantalum Capacitor [capacitance=47µF voltage=10V part_number=TAJB476K006RNJ package="B 3528 [SMD, tantalum]"]
  C15 = Ceramic Capacitor [capacitance=0.1µF voltage=50V part_number=C1206C104K5RAC7867 package="1206 [SMD, multilayer]"]
  R62 = Resistor [tolerance=±5% resistance=100k package="0805 [SMD]"]
  R63 = Resistor [tolerance=±5% resistance=100k package="0805 [SMD]"]
  R64 = Resistor [tolerance=±1% resistance=1k part_number=RC0805FR-071KL package="0805 [SMD]"]
  R65 = Resistor [tolerance=±1% resistance=1k part_number=RC0805FR-071KL package="0805 [SMD]"]
  IC3 = SO08 [chip_label=SO08 part_number=VNLD5090-E package=SO]
  LED4 = smd LED [color="Red (633nm)" part_number="LH R974-LP-1" package="0805 [SMD]"]
  R15 = Resistor [tolerance=±5% resistance=2.4k package="0805 [SMD]"]
  LED3 = smd LED [color="Red (633nm)" part_number="LH R974-LP-1" package="0805 [SMD]"]
  IC6 = SO16 [chip_label=SP720ABTG part_number=SP720ABTG package=SO]
  C3 = Ceramic Capacitor [capacitance=0.1µF part_number=CL21F104ZBCNNNC package="0805 [SMD, multilayer]"]
  C1 = Ceramic Capacitor [capacitance=0.1µF part_number=CL21F104ZBCNNNC package="0805 [SMD, multilayer]"]
  C7 = Ceramic Capacitor [capacitance=0.1µF part_number=CL21F104ZBCNNNC package="0805 [SMD, multilayer]"]
  C5 = Ceramic Capacitor [capacitance=0.1µF part_number=CL21F104ZBCNNNC package="0805 [SMD, multilayer]"]
  C9 = Ceramic Capacitor [capacitance=0.1µF part_number=CL21F104ZBCNNNC package="0805 [SMD, multilayer]"]
  C26 = Ceramic Capacitor [capacitance=0.1µF part_number=CL21F104ZBCNNNC package="0805 [SMD, multilayer]"]
  C27 = Ceramic Capacitor [capacitance=0.1µF part_number=CL21F104ZBCNNNC package="0805 [SMD, multilayer]"]
  R3 = Resistor [tolerance=±0.1% resistance=2.49k package="0805 [SMD]"]
  R1 = Resistor [tolerance=±0.1% resistance=2.49k package="0805 [SMD]"]
  R8 = Resistor [tolerance=±5% resistance=470 package="0805 [SMD]"]
  R18 = Resistor [tolerance=±5% resistance=2.4k package="0805 [SMD]"]
  R23 = Resistor [tolerance=±1% resistance=1k part_number=RC0805FR-071KL package="0805 [SMD]"]
  R24 = Resistor [tolerance=±1% resistance=1k part_number=RC0805FR-071KL package="0805 [SMD]"]
  R29 = Resistor [tolerance=±1% resistance=1k part_number=RC0805FR-071KL package="0805 [SMD]"]
  R30 = Resistor [tolerance=±1% resistance=1k part_number=RC0805FR-071KL package="0805 [SMD]"]
  Part30 = 174917_DENSO-ECU-socket_48pin-040-070 [part_number=174917 package="48-pin 0.40/0.70"]
  D19 = Diode [part_number=1N4448WX-TP package=sod-323]
  D18 = Diode [part_number=1N4448WX-TP package=sod-323]
  D21 = Diode [part_number=1N4448WX-TP package=sod-323]
  D20 = Diode [part_number=1N4448WX-TP package=sod-323]
  LED1 = smd LED [color="Red (633nm)" part_number="LH R974-LP-1" package="0805 [SMD]"]
  MPX4250AP = MPX4250AP pressure sensor [part_number=MPX]
  R4 = Resistor [tolerance=±5% resistance=470 package="0805 [SMD]"]
  R39 = Resistor [tolerance=±5% resistance=1k package="0805 [SMD]"]
  R66 = Resistor [tolerance=±5% resistance=220 package="0805 [SMD]"]
  LED8 = smd LED [color="Red (633nm)" package="0805 [SMD]"]
  LED7 = smd LED [color="Red (633nm)" part_number="LH R974-LP-1" package="0805 [SMD]"]
  LED5 = smd LED [color="Red (633nm)" part_number="LH R974-LP-1" package="0805 [SMD]"]
  LED6 = smd LED [color="Red (633nm)" part_number="LH R974-LP-1" package="0805 [SMD]"]
  R26 = Resistor [tolerance=±5% resistance=2.4k package="0805 [SMD]"]
  R36 = Resistor [tolerance=±5% resistance=100k package="0805 [SMD]"]
  R67 = Resistor [tolerance=±5% resistance=220 package="0805 [SMD]"]
  R40 = Resistor [tolerance=±5% resistance=1k package="0805 [SMD]"]
  R28 = Resistor [tolerance=±5% resistance=2.4k package="0805 [SMD]"]
  R38 = Resistor [tolerance=±5% resistance=100k package="0805 [SMD]"]
  R34 = Resistor [tolerance=±5% resistance=2.4k package="0805 [SMD]"]
  R33 = Resistor [tolerance=±5% resistance=2.4k power=0.25W package="0805 [SMD]"]
  C16 = Tantalum Capacitor [capacitance=10µF voltage=35V part_number=T491D106K050AT package="D 7343 [SMD, tantalum]"]
  U6 = DIODE-ZENER [package=diode-zener]
  R54 = Resistor [tolerance=±5% resistance=10k package="0805 [SMD]"]
  R2 = Resistor [tolerance=±5% resistance=470 package="0805 [SMD]"]
  C2 = Ceramic Capacitor [capacitance=0.22µF package="0805 [SMD, multilayer]"]
  R22 = Resistor [tolerance=±5% resistance=470 package="0805 [SMD]"]
  C10 = Ceramic Capacitor [capacitance=0.22µF package="0805 [SMD, multilayer]"]
  C23 = Ceramic Capacitor [capacitance=4.7nF package="0805 [SMD, multilayer]"]
  D23 = Diode [part_number=B0540WS-7 package=sod-323]
  C12 = Ceramic Capacitor [capacitance=1µF package="0805 [SMD, multilayer]"]
  C4 = Ceramic Capacitor [capacitance=0.22µF package="0805 [SMD, multilayer]"]
  C6 = Ceramic Capacitor [capacitance=0.22µF package="0805 [SMD, multilayer]"]
  R6 = Resistor [tolerance=±5% resistance=470 package="0805 [SMD]"]
  R7 = Resistor [tolerance=±0.1% resistance=3.9k package="0805 [SMD]"]
  R21 = Resistor [tolerance=±5% resistance=1k package="0805 [SMD]"]
  C8 = Ceramic Capacitor [capacitance=0.22µF package="0805 [SMD, multilayer]"]
  U7 = DIODE-ZENER [package=diode-zener]
  R68 = Resistor [tolerance=±5% resistance=10 part_number=RC0805FR-0710RL package="0805 [SMD]"]
  R69 = Resistor [tolerance=±5% resistance=10 part_number=RC0805FR-0710RL package="0805 [SMD]"]
  R70 = Resistor [tolerance=±5% resistance=1k package="0805 [SMD]"]
  U8 = DIODE-ZENER [part_number=MM3Z5V1ST1G package=sod-323]
  R41 = Resistor [tolerance=±5% resistance=750 package="0805 [SMD]"]
  C18 = Ceramic Capacitor [capacitance=0.3µF package="0805 [SMD, multilayer]"]
  C20 = Ceramic Capacitor [capacitance=1µF package="0805 [SMD, multilayer]"]
  IC5 = SO08 [chip_label=SO08 part_number=VNLD5090-E package=SO]
  R55 = Resistor [tolerance=±5% resistance=100k package="0805 [SMD]"]
  R57 = Resistor [tolerance=±5% resistance=1k part_number=RC0805FR-071KL package="0805 [SMD]"]
  R58 = Resistor [tolerance=±5% resistance=1k part_number=RC0805FR-071KL package="0805 [SMD]"]
  R56 = Resistor [tolerance=±5% resistance=100k power=0.25W package="0805 [SMD]"]
  DRV8825_Stepper = Pololu A4988 [package=SO16]
  C19 = Ceramic Capacitor [capacitance=0.01µF package="0805 [SMD, multilayer]"]
  J1 = female pin header, 1 pin [form="♀ (female)"]  # not connected
  J2 = female pin header, 1 pin [form="♀ (female)"]  # not connected
  J3 = female pin header, 1 pin [form="♀ (female)"]  # not connected
  J4 = female pin header, 1 pin [form="♀ (female)"]  # not connected
  J6 = female pin header, 1 pin [form="♀ (female)"]  # not connected
  J7 = female pin header, 1 pin [form="♀ (female)"]  # not connected
  J8 = female pin header, 1 pin [form="♀ (female)"]  # not connected
  J9 = female pin header, 1 pin [form="♀ (female)"]  # not connected
  J10 = female pin header, 1 pin [form="♀ (female)"]  # not connected
  J11 = female pin header, 1 pin [form="♀ (female)"]  # not connected
  J12 = female pin header, 1 pin [form="♀ (female)"]  # not connected
  J13 = female pin header, 1 pin [form="♀ (female)"]  # not connected
  J14 = female pin header, 1 pin [form="♀ (female)"]  # not connected
  J15 = female pin header, 1 pin [form="♀ (female)"]  # not connected
  J16 = female pin header, 1 pin [form="♀ (female)"]  # not connected
  J17 = female pin header, 1 pin [form="♀ (female)"]  # not connected
  J18 = female pin header, 1 pin [form="♀ (female)"]  # not connected
  J19 = female pin header, 1 pin [form="♀ (female)"]  # not connected
  J20 = female pin header, 1 pin [form="♀ (female)"]  # not connected
  J21 = female pin header, 1 pin [form="♀ (female)"]  # not connected
  J22 = female pin header, 1 pin [form="♀ (female)"]  # not connected
  J23 = female pin header, 1 pin [form="♀ (female)"]  # not connected
  J24 = female pin header, 1 pin [form="♀ (female)"]  # not connected
  J25 = female pin header, 1 pin [form="♀ (female)"]  # not connected
  J26 = female pin header, 1 pin [form="♀ (female)"]  # not connected
  J27 = female pin header, 1 pin [form="♀ (female)"]  # not connected
  J28 = female pin header, 1 pin [form="♀ (female)"]  # not connected
  J29 = female pin header, 1 pin [form="♀ (female)"]  # not connected
  J30 = female pin header, 1 pin [form="♀ (female)"]  # not connected
  J31 = female pin header, 1 pin [form="♀ (female)"]  # not connected
  J32 = female pin header, 1 pin [form="♀ (female)"]  # not connected
  J33 = female pin header, 1 pin [form="♀ (female)"]  # not connected
  J34 = female pin header, 1 pin [form="♀ (female)"]  # not connected
  J35 = female pin header, 1 pin [form="♀ (female)"]  # not connected
  J36 = female pin header, 1 pin [form="♀ (female)"]  # not connected
  J37 = female pin header, 1 pin [form="♀ (female)"]  # not connected
  J38 = female pin header, 1 pin [form="♀ (female)"]  # not connected
  J39 = female pin header, 1 pin [form="♀ (female)"]  # not connected
  J40 = female pin header, 1 pin [form="♀ (female)"]  # not connected
  J41 = female pin header, 1 pin [form="♀ (female)"]  # not connected
  J42 = female pin header, 1 pin [form="♀ (female)"]  # not connected
  J43 = female pin header, 1 pin [form="♀ (female)"]  # not connected
  J44 = female pin header, 1 pin [form="♀ (female)"]  # not connected
  J45 = female pin header, 1 pin [form="♀ (female)"]  # not connected
  J46 = female pin header, 1 pin [form="♀ (female)"]  # not connected
  J47 = female pin header, 1 pin [form="♀ (female)"]  # not connected
  J48 = female pin header, 1 pin [form="♀ (female)"]  # not connected
  J49 = female pin header, 1 pin [form="♀ (female)"]  # not connected
  J50 = female pin header, 1 pin [form="♀ (female)"]  # not connected
  J51 = female pin header, 1 pin [form="♀ (female)"]  # not connected
  J52 = female pin header, 1 pin [form="♀ (female)"]  # not connected
  J53 = female pin header, 1 pin [form="♀ (female)"]  # not connected
  J54 = female pin header, 1 pin [form="♀ (female)"]  # not connected
  J55 = female pin header, 1 pin [form="♀ (female)"]  # not connected
  J56 = female pin header, 1 pin [form="♀ (female)"]  # not connected
  J57 = female pin header, 1 pin [form="♀ (female)"]  # not connected
  J58 = female pin header, 1 pin [form="♀ (female)"]  # not connected
  J59 = female pin header, 1 pin [form="♀ (female)"]  # not connected
  J60 = female pin header, 1 pin [form="♀ (female)"]  # not connected
  J61 = female pin header, 1 pin [form="♀ (female)"]  # not connected
  J62 = female pin header, 1 pin [form="♀ (female)"]  # not connected
  J63 = female pin header, 1 pin [form="♀ (female)"]  # not connected
  J64 = female pin header, 1 pin [form="♀ (female)"]  # not connected
  J65 = female pin header, 1 pin [form="♀ (female)"]  # not connected
  J66 = female pin header, 1 pin [form="♀ (female)"]  # not connected
  J67 = female pin header, 1 pin [form="♀ (female)"]  # not connected
  J68 = female pin header, 1 pin [form="♀ (female)"]
  J69 = female pin header, 1 pin [form="♀ (female)"]
  J70 = female pin header, 1 pin [form="♀ (female)"]
  J71 = female pin header, 1 pin [form="♀ (female)"]
  J72 = female pin header, 1 pin [form="♀ (female)"]
  J73 = female pin header, 1 pin [form="♀ (female)"]
  5V = female pin header, 7 pins [form="♀ (female)"]
  GND = female pin header, 7 pins [form="♀ (female)"]
  J74 = female pin header, 1 pin [form="♀ (female)"]  # not connected
  J75 = female pin header, 1 pin [form="♀ (female)"]  # not connected
  J76 = female pin header, 1 pin [form="♀ (female)"]  # not connected
  J77 = female pin header, 1 pin [form="♀ (female)"]
  J78 = female pin header, 1 pin [form="♀ (female)"]  # not connected
  J79 = female pin header, 1 pin [form="♀ (female)"]  # not connected
  J80 = female pin header, 1 pin [form="♀ (female)"]  # not connected
  J81 = female pin header, 1 pin [form="♀ (female)"]  # not connected
  J82 = female pin header, 1 pin [form="♀ (female)"]  # not connected
  J83 = female pin header, 1 pin [form="♀ (female)"]  # not connected
  J84 = female pin header, 1 pin [form="♀ (female)"]  # not connected
  J85 = female pin header, 1 pin [form="♀ (female)"]  # not connected
  HC-05_B/T = female pin header, 6 pins [form="♀ (female)"]
  SPI = female pin header, 3 pins [form="♀ (female)"]
  I2C = female pin header, 2 pins [form="♀ (female)"]
  J86 = female pin header, 3 pins [form="♀ (female)"]
  F1 = Resettable Fuse PTC [part_number=0ZCJ0075AF2E package=ptc-1206]
  SJ1 = Solder Jumper [package=sj_2s]

nets (from the schematic view):
  CPU-A8: Arduino_Mega_2560.A8, J69.pin1
  CPU-A9: Arduino_Mega_2560.A9, IC7.36
  CPU-A10: Arduino_Mega_2560.A10, IC7.35
  ADC Clamp1/IAT-CPU-A0: Arduino_Mega_2560.A0, IC6.1, R2.Pin_1, C2.1
  ADC Clamp2/CLT-CPU-A1: Arduino_Mega_2560.A1, IC6.2, R4.Pin_1, C4.1
  ADC Clamp3/TPS-CPU-A2: Arduino_Mega_2560.A2, IC6.3, C6.1, R6.Pin_1
  ADC Clamp4/CPU-A3: Arduino_Mega_2560.A3, IC6.4, R22.Pin_1, C10.1
  ADC Clamp5/BRV-CPU-A4: Arduino_Mega_2560.A4, IC6.5, R8.Pin_1, C8.1
  ADC Clamp6/CPU-A5: Arduino_Mega_2560.A5, IC6.6, R41.Pin_1, C18.0
  33814-CSB/CPU-A6: Arduino_Mega_2560.A6, IC7.10
  SCL-CPU-D21: Arduino_Mega_2560.D21/SCL, Arduino_Mega_2560.SCL, I2C.pin2
  SDA-CPU-D20: Arduino_Mega_2560.D20/SDA, Arduino_Mega_2560.SDA, I2C.pin1
  ADC Clamp8/TACH1-CPU-D19: Arduino_Mega_2560.D19/RX1, IC6.15, C26.0, R66.Pin_1
  ADC Clamp9/TACH2-CPU-D18: Arduino_Mega_2560.D18/TX1, IC6.14, C27.1, R67.Pin_1
  STEP-CPU-D17: Arduino_Mega_2560.D17_PWM/RX2, DRV8825_Stepper.STEP
  STEPDIR-CPU-D16: Arduino_Mega_2560.D16_PWM/TX2, DRV8825_Stepper.DIR
  CPU-D12: Arduino_Mega_2560.D12_PWM, R70.Pin_1, U8.C
  CPU-D11: Arduino_Mega_2560.D11_PWM, R59.Pin_0, R61.Pin_0
  CPU-D10: Arduino_Mega_2560.D10_PWM, R17.Pin_0, R60.Pin_0
  CPU-D9: Arduino_Mega_2560.D9_PWM, R62.Pin_0, R64.Pin_0
  CPU-D8: Arduino_Mega_2560.D8_PWM, R63.Pin_0, R65.Pin_0
  5V/VCC: Arduino_Mega_2560.IOREF, Arduino_Mega_2560.5V, IC7.17, IC1.6, C14.+, C13.1, IC6.16, R39.Pin_0, R40.Pin_0, U6.C, R54.Pin_0, D23.C, C12.1, DRV8825_Stepper.RESET, DRV8825_Stepper.SLEEP, 5V.pin1, 5V.pin2, 5V.pin3, 5V.pin4, 5V.pin5, 5V.pin6, 5V.pin7, HC-05_B/T.pin2, J86.pin3
  RESET: Arduino_Mega_2560.RESET, R54.Pin_1, C23.1, D23.A, SJ1.2
  GND: Arduino_Mega_2560.GND, U2.P$2, IC7.15, IC7.22, IC7.38, IC7.40, IC7.42, IC2.3, IC1.3, R35.Pin_0, R37.Pin_0, IC4.5, IC4.7, R17.Pin_1, R61.Pin_1, C14.-, C13.0, C24.0, C25.-, C15.0, R62.Pin_1, R63.Pin_1, IC3.5, IC3.7, IC6.8, C3.0, C1.0, C7.0, C5.0, C9.0, C26.1, C27.0, Part30.2A, Part30.2B, Part30.2C, Part30.2D, MPX4250AP.GND, LED8.cathode, LED7.cathode, LED5.cathode, LED6.cathode, R36.Pin_0, R38.Pin_0, C16.-, U6.A, C2.0, C10.0, C23.0, C12.0, C4.0, C6.0, R21.Pin_1, C8.0, U7.A, U8.A, C18.1, C20.0, IC5.5, IC5.7, R55.Pin_0, R56.Pin_0, DRV8825_Stepper.GND, C19.0, GND.pin1, GND.pin2, GND.pin3, GND.pin4, GND.pin5, GND.pin6, GND.pin7, HC-05_B/T.pin3
  CPU-D0: Arduino_Mega_2560.D0_RX0, HC-05_B/T.pin4
  CPU-D1: Arduino_Mega_2560.D1_TX0, HC-05_B/T.pin5
  CPU-D2: Arduino_Mega_2560.D2_PWM, R57.Pin_0
  CPU-D4: Arduino_Mega_2560.D4_PWM, R58.Pin_0
  CPU-D5: Arduino_Mega_2560.D5_PWM
  CPU-D6: Arduino_Mega_2560.D6_PWM
  LS1-CPU-D7: Arduino_Mega_2560.D7_PWM
  FP-CPU-D22: Arduino_Mega_2560.D22
  CPU-D23: Arduino_Mega_2560.D23, HC-05_B/T.pin1
  CPU-D35: Arduino_Mega_2560.D35, R29.Pin_0
  CPU-D37: Arduino_Mega_2560.D37, R30.Pin_0
  IGN2-CPU-D24: Arduino_Mega_2560.D38
  CPU-D39: Arduino_Mega_2560.D39, R23.Pin_0
  IGN1-CPU-D28: Arduino_Mega_2560.D40
  CPU-D41: Arduino_Mega_2560.D41, R24.Pin_0
  RST-CPU-D48: Arduino_Mega_2560.D43
  CPU-D44: Arduino_Mega_2560.D44, J68.pin1
  LC-CPU-D45: Arduino_Mega_2560.D45
  CPU-D46: Arduino_Mega_2560.D46, J73.pin1
  CPU-D47: Arduino_Mega_2560.D47
  CPU-D48: Arduino_Mega_2560.D48, J72.pin1
  CPU-D49: Arduino_Mega_2560.D49
  MISO: Arduino_Mega_2560.D50, IC7.16, SPI.pin2
  MOSI: Arduino_Mega_2560.D51, IC7.13, SPI.pin1
  SCLK: Arduino_Mega_2560.D52, IC7.12, SPI.pin3
  CPU-D53: Arduino_Mega_2560.D53
  VRegIn: D15.cathode, IC7.11
  12V: D15.anode, U2.P$1, R12.Pin_0, R9.Pin_0, C15.1, R15.Pin_0, R18.Pin_0, Part30.1B, C16.+, R7.Pin_0, DRV8825_Stepper.VMOT, J70.pin1, J86.pin1
  VRSOut: IC7.7
  VRSP: IC7.8
  VRSN: IC7.9
  N1: IC7.19, SJ1.1
  VPROT: IC7.20, C24.1, C25.+, R3.Pin_0, R1.Pin_0, Part30.1N, MPX4250AP.Vs, U7.C, C20.1, C19.1
  ROUT2: IC7.23, J71.pin1
  FP-Out: IC7.41, Part30.2O
  N2: IC2.2, R29.Pin_1, R38.Pin_1
  N3: IC2.4, R30.Pin_1, R36.Pin_1
  N4: IC2.5, R34.Pin_1, F1.1
  N5: IC2.6, J86.pin2
  N6: IC2.7, R33.Pin_1
  N7: IC1.2, R37.Pin_1, R23.Pin_1
  N8: IC1.4, R35.Pin_1, R24.Pin_1
  N9: IC1.5, R26.Pin_1, R68.Pin_0
  N10: IC1.7, R28.Pin_1, R69.Pin_1
  N11: IC4.1, R59.Pin_1
  N12: IC4.3, R60.Pin_1
  INJ-2-OUT: IC4.6, Part30.2V, D19.C
  INJ-1-OUT: IC4.8, Part30.2U, D18.C
  N13: R12.Pin_1, LED2.anode
  N14: R9.Pin_1, LED1.anode
  N15: LED2.cathode, D19.A
  N16: R64.Pin_1, IC3.1
  N17: R65.Pin_1, IC3.3
  INJ-4-OUT: IC3.6, D21.C
  INJ-3-OUT: IC3.8, D20.C
  N18: LED4.cathode, D21.A
  N19: LED4.anode, R18.Pin_1
  N20: R15.Pin_1, LED3.anode
  N21: LED3.cathode, D20.A
  ADC Clamp7: IC6.7
  ADC Clamp14: IC6.9
  ADC Clamp13: IC6.10
  ADC Clamp12: IC6.11
  ADC Clamp11: IC6.12
  ADC Clamp10: IC6.13
  CLT Sensor: C3.1, R3.Pin_1, Part30.2Q, R4.Pin_0
  IAT Sensor: C1.1, R1.Pin_1, Part30.2P, R2.Pin_0
  N22: C7.1, R8.Pin_0, R7.Pin_1, R21.Pin_0
  TPS Sensor: C5.1, Part30.2L, R6.Pin_0
  O2 Sensor: C9.1, Part30.2N, R22.Pin_0
  ST_Sig: Part30.1C, F1.2
  IGN-1-OUT: Part30.1G, R69.Pin_0
  IGN-2-OUT: Part30.1H, R68.Pin_1
  Clutch in: Part30.1V, R70.Pin_0
  Crank: Part30.2E, R39.Pin_1, R66.Pin_0
  Cam: Part30.2G, R67.Pin_0, R40.Pin_1
  IDLE-OUT: Part30.2W, IC5.8
  N23: D18.A, LED1.cathode
  N24: MPX4250AP.V_out, R41.Pin_0
  N25: LED8.anode, R34.Pin_0
  N26: LED7.anode, R33.Pin_0
  N27: LED5.anode, R28.Pin_0
  N28: LED6.anode, R26.Pin_0
  N29: IC5.1, R55.Pin_1, R57.Pin_1
  N30: IC5.3, R58.Pin_1, R56.Pin_1
  BOOST-OUT: IC5.6, J77.pin1
  STEP-1B-OUT: DRV8825_Stepper.1B
  STEP-1A-OUT: DRV8825_Stepper.1A
  STEP-2A-OUT: DRV8825_Stepper.2A
  STEP-2B-OUT: DRV8825_Stepper.2B

notes:
  Speeduino Pro, Inlet Air Temperature sensor
  Coolant Temperature Sensor
  Speeduino Pro, Throttle Position Sensor
  Battery Reference Voltage
  Speeduino Pro v1, Injectors
  Speeduino v0.4, O2 Sensor
  Ignitor output 1
  Ignitor output 2
  Power supply
  Crank and Cam sensors
  Speeduino Pro, MAP sensor input
  Speeduino MX5 PNP v1
  PWM Idle / Boost
  inj1
  Reset Protection - Refer AVR040 Application note
  ADC Clamping circuit
  Stepper Driver
  TAPR 1.0
  © Josh Stewart
  Arduino Mega 2560
  MC33814
  2A
  1A
  Proto Area
  Clutch input
  Boost
  A8
  12v
  Bluetooth Connector
  5V
  GND
  RX
  TX
  D20
  D21
  D44
  D48
  D46
  5v
