# Fritzing sketch speeduino pro NA8 64-pin (saved by Fritzing 0.9.3b)
circuit board: 10cm x 12cm
breadboards: 1

parts:
  Arduino_Mega_2560 = Arduino Mega 2560 (Rev3) [part_number="Arduino Mega 2560"]
  D5 = Schottky Diode [part_number=1N5818 package="300 mil [THT]"]
  U2 = V18ZA2P [part_number=ERZV14D220 package=v18za2p]
  IC7 = LQFP-48 [chip_label=LQFP-48 part_number=MC33814 package=LQFP]
  IC1 = SO08 [chip_label=IC part_number=TC4424AVOA package=SO]
  R30 = Resistor [tolerance=±5% resistance=100k part_number=RC0805FR-07100KL package="0805 [SMD]"]
  R31 = Resistor [tolerance=±5% resistance=100k part_number=RC0805FR-07100KL package="0805 [SMD]"]
  IC4 = SO08 [chip_label=SO08 part_number=VNLD5090-E package=SO]
  R19 = Resistor [tolerance=±5% resistance=100k part_number=RC0805FR-07100KL package="0805 [SMD]"]
  R14 = Resistor [tolerance=±1% resistance=1k part_number=RC0805FR-071KL package="0805 [SMD]"]
  R15 = Resistor [tolerance=±1% resistance=1k part_number=RC0805FR-071KL package="0805 [SMD]"]
  R18 = Resistor [tolerance=±5% resistance=100k part_number=RC0805FR-07100KL package="0805 [SMD]"]
  R11 = Resistor [tolerance=±5% resistance=2.4k power=0.25W part_number=RC0805FR-072K4L package="0805 [SMD]"]
  R10 = Resistor [tolerance=±5% resistance=2.4k part_number=RC0805FR-072K4L package="0805 [SMD]"]
  LED2 = smd LED [color="Red (633nm)" part_number="LH R974-LP-1" package="0805 [SMD]"]
  C15 = Tantalum Capacitor [capacitance=47µF voltage=10V part_number=TAJB476K006RNJ package="B 3528 [SMD, tantalum]"]
  C13 = Ceramic Capacitor [capacitance=0.1µF voltage=50V part_number=C1206C104K5RAC7867 package="1206 [SMD, multilayer]"]
  C14 = Ceramic Capacitor [capacitance=0.1µF voltage=50V part_number=C1206C104K5RAC7867 package="1206 [SMD, multilayer]"]
  C16 = Tantalum Capacitor [capacitance=47µF voltage=10V part_number=TAJB476K006RNJ package="B 3528 [SMD, tantalum]"]
  C17 = Ceramic Capacitor [capacitance=0.1µF voltage=50V part_number=C1206C104K5RAC7867 package="1206 [SMD, multilayer]"]
  R20 = Resistor [tolerance=±5% resistance=100k part_number=RC0805FR-07100KL package="0805 [SMD]"]
  R21 = Resistor [tolerance=±5% resistance=100k part_number=RC0805FR-07100KL package="0805 [SMD]"]
  R16 = Resistor [tolerance=±1% resistance=1k part_number=RC0805FR-071KL package="0805 [SMD]"]
  R17 = Resistor [tolerance=±1% resistance=1k part_number=RC0805FR-071KL package="0805 [SMD]"]
  IC3 = SO08 [chip_label=SO08 part_number=VNLD5090-E package=SO]
  LED4 = smd LED [color="Red (633nm)" part_number="LH R974-LP-1" package="0805 [SMD]"]
  R12 = Resistor [tolerance=±5% resistance=2.4k part_number=RC0805FR-072K4L package="0805 [SMD]"]
  LED3 = smd LED [color="Red (633nm)" part_number="LH R974-LP-1" package="0805 [SMD]"]
  IC6 = SO16 [chip_label=SP720ABTG part_number=SP720ABTG package=SO]
  C3 = Ceramic Capacitor [capacitance=0.1µF part_number=CL21F104ZBCNNNC package="0805 [SMD, multilayer]"]
  C1 = Ceramic Capacitor [capacitance=0.1µF part_number=CL21F104ZBCNNNC package="0805 [SMD, multilayer]"]
  C7 = Ceramic Capacitor [capacitance=0.1µF part_number=CL21F104ZBCNNNC package="0805 [SMD, multilayer]"]
  C5 = Ceramic Capacitor [capacitance=0.1µF part_number=CL21F104ZBCNNNC package="0805 [SMD, multilayer]"]
  C9 = Ceramic Capacitor [capacitance=0.1µF part_number=CL21F104ZBCNNNC package="0805 [SMD, multilayer]"]
  C23 = Ceramic Capacitor [capacitance=0.1µF part_number=CL21F104ZBCNNNC package="0805 [SMD, multilayer]"]
  C22 = Ceramic Capacitor [capacitance=0.1µF part_number=CL21F104ZBCNNNC package="0805 [SMD, multilayer]"]
  R3 = Resistor [tolerance=±0.1% resistance=2.49k part_number=RT0805BRD072K49L package="0805 [SMD]"]
  R1 = Resistor [tolerance=±0.1% resistance=2.49k part_number=RT0805BRD072K49L package="0805 [SMD]"]
  R8 = Resistor [tolerance=±1% resistance=470 part_number=ERJ-6ENF4700V package="0805 [SMD]"]
  R13 = Resistor [tolerance=±5% resistance=2.4k part_number=RC0805FR-072K4L package="0805 [SMD]"]
  R24 = Resistor [tolerance=±1% resistance=1k part_number=RC0805FR-071KL package="0805 [SMD]"]
  R25 = Resistor [tolerance=±1% resistance=1k part_number=RC0805FR-071KL package="0805 [SMD]"]
  D3 = Diode [part_number=1N4448WX-TP package=sod-323]
  D4 = Diode [part_number=1N4448WX-TP package=sod-323]
  D1 = Diode [part_number=1N4448WX-TP package=sod-323]
  D2 = Diode [part_number=1N4448WX-TP package=sod-323]
  LED1 = smd LED [color="Red (633nm)" part_number="LH R974-LP-1" package="0805 [SMD]"]
  R4 = Resistor [tolerance=±1% resistance=470 part_number=ERJ-6ENF4700V package="0805 [SMD]"]
  R37 = Resistor [tolerance=±5% resistance=1k part_number=RC0805FR-071KL package="0805 [SMD]"]
  R35 = Resistor [tolerance=±5% resistance=220 part_number=RC0805FR-07220RL package="0805 [SMD]"]
  LED5 = smd LED [color="Red (633nm)" part_number="LH R974-LP-1" package="0805 [SMD]"]
  LED6 = smd LED [color="Red (633nm)" part_number="LH R974-LP-1" package="0805 [SMD]"]
  R27 = Resistor [tolerance=±5% resistance=2.4k part_number=RC0805FR-072K4L package="0805 [SMD]"]
  R34 = Resistor [tolerance=±5% resistance=220 part_number=RC0805FR-07220RL package="0805 [SMD]"]
  R36 = Resistor [tolerance=±5% resistance=1k part_number=RC0805FR-071KL package="0805 [SMD]"]
  R26 = Resistor [tolerance=±5% resistance=2.4k part_number=RC0805FR-072K4L package="0805 [SMD]"]
  C18 = Tantalum Capacitor [capacitance=10µF voltage=35V part_number=T491D106K050AT package="D 7343 [SMD, tantalum]"]
  U6 = DIODE-ZENER [part_number=1N5919BG package=diode-zener]
  R39 = Resistor [tolerance=±5% resistance=10k package="0805 [SMD]"]
  R2 = Resistor [tolerance=±1% resistance=470 part_number=ERJ-6ENF4700V package="0805 [SMD]"]
  C2 = Ceramic Capacitor [capacitance=0.22µF part_number=CL21B224KOCNNNC package="0805 [SMD, multilayer]"]
  R9 = Resistor [tolerance=±5% resistance=470 part_number=ERJ-6ENF4700V package="0805 [SMD]"]
  C10 = Ceramic Capacitor [capacitance=0.22µF part_number=CL21B224KOCNNNC package="0805 [SMD, multilayer]"]
  C11 = Ceramic Capacitor [capacitance=4.7nF part_number=CC0805KRX7R9BB472 package="0805 [SMD, multilayer]"]
  D6 = Diode [part_number=B0540WS-7 package=sod-323]
  C4 = Ceramic Capacitor [capacitance=0.22µF part_number=CL21B224KOCNNNC package="0805 [SMD, multilayer]"]
  C6 = Ceramic Capacitor [capacitance=0.22µF part_number=CL21B224KOCNNNC package="0805 [SMD, multilayer]"]
  R5 = Resistor [tolerance=±5% resistance=470 part_number=ERJ-6ENF4700V package="0805 [SMD]"]
  R7 = Resistor [tolerance=±1% resistance=3.9k part_number=RC0805FR-073K9L package="0805 [SMD]"]
  R6 = Resistor [tolerance=±5% resistance=1k part_number=RC0805FR-071KL package="0805 [SMD]"]
  C8 = Ceramic Capacitor [capacitance=0.22µF part_number=CL21B224KOCNNNC package="0805 [SMD, multilayer]"]
  U7 = DIODE-ZENER [part_number=1N5919BG package=diode-zener]
  R44 = Resistor [tolerance=±5% resistance=10 part_number=RC0805FR-0710RL package="0805 [SMD]"]
  R45 = Resistor [tolerance=±5% resistance=10 part_number=RC0805FR-0710RL package="0805 [SMD]"]
  R46 = Resistor [tolerance=±5% resistance=1k part_number=RC0805FR-071KL package="0805 [SMD]"]
  U8 = DIODE-ZENER [part_number=MM3Z5V1ST1G package=sod-323]
  R38 = Resistor [tolerance=±5% resistance=470 part_number=ERJ-6ENF4700V package="0805 [SMD]"]
  C19 = Ceramic Capacitor [capacitance=470pF part_number=CC0805KRX7R9BB471 package="0805 [SMD, multilayer]"]
  C20 = Ceramic Capacitor [capacitance=1µF part_number=CC0805KKX7R7BB105 package="0805 [SMD, multilayer]"]
  IC5 = SO08 [chip_label=SO08 part_number=VNLD5090-E package=SO]
  R43 = Resistor [tolerance=±5% resistance=100k part_number=RC0805FR-07100KL package="0805 [SMD]"]
  R42 = Resistor [tolerance=±5% resistance=1k part_number=RC0805FR-071KL package="0805 [SMD]"]
  R40 = Resistor [tolerance=±5% resistance=1k part_number=RC0805FR-071KL package="0805 [SMD]"]
  R41 = Resistor [tolerance=±5% resistance=100k power=0.25W part_number=RC0805FR-07100KL package="0805 [SMD]"]
  DRV8825_Stepper = Pololu A4988 [package=SO16]
  C21 = Ceramic Capacitor [capacitance=0.01µF part_number=CC0805KRX7R9BB103 package="0805 [SMD, multilayer]"]
  J1 = female pin header, 1 pin [form="♀ (female)"]  # not connected
  J2 = female pin header, 1 pin [form="♀ (female)"]  # not connected
  J3 = female pin header, 1 pin [form="♀ (female)"]  # not connected
  J4 = female pin header, 1 pin [form="♀ (female)"]  # not connected
  J6 = female pin header, 1 pin [form="♀ (female)"]  # not connected
  J7 = female pin header, 1 pin [form="♀ (female)"]  # not connected
  J8 = female pin header, 1 pin [form="♀ (female)"]  # not connected
  J9 = female pin header, 1 pin [form="♀ (female)"]  # not connected
  J10 = female pin header, 1 pin [form="♀ (female)"]  # not connected
  J11 = female pin header, 1 pin [form="♀ (female)"]  # not connected
  J12 = female pin header, 1 pin [form="♀ (female)"]  # not connected
  J13 = female pin header, 1 pin [form="♀ (female)"]  # not connected
  J14 = female pin header, 1 pin [form="♀ (female)"]  # not connected
  J15 = female pin header, 1 pin [form="♀ (female)"]  # not connected
  J16 = female pin header, 1 pin [form="♀ (female)"]  # not connected
  J17 = female pin header, 1 pin [form="♀ (female)"]  # not connected
  J18 = female pin header, 1 pin [form="♀ (female)"]  # not connected
  J19 = female pin header, 1 pin [form="♀ (female)"]  # not connected
  J20 = female pin header, 1 pin [form="♀ (female)"]  # not connected
  J21 = female pin header, 1 pin [form="♀ (female)"]  # not connected
  J22 = female pin header, 1 pin [form="♀ (female)"]  # not connected
  J23 = female pin header, 1 pin [form="♀ (female)"]  # not connected
  J24 = female pin header, 1 pin [form="♀ (female)"]  # not connected
  J25 = female pin header, 1 pin [form="♀ (female)"]  # not connected
  J26 = female pin header, 1 pin [form="♀ (female)"]  # not connected
  J27 = female pin header, 1 pin [form="♀ (female)"]  # not connected
  J28 = female pin header, 1 pin [form="♀ (female)"]  # not connected
  J29 = female pin header, 1 pin [form="♀ (female)"]  # not connected
  J30 = female pin header, 1 pin [form="♀ (female)"]  # not connected
  J31 = female pin header, 1 pin [form="♀ (female)"]  # not connected
  J32 = female pin header, 1 pin [form="♀ (female)"]  # not connected
  J33 = female pin header, 1 pin [form="♀ (female)"]  # not connected
  J34 = female pin header, 1 pin [form="♀ (female)"]  # not connected
  J35 = female pin header, 1 pin [form="♀ (female)"]  # not connected
  J36 = female pin header, 1 pin [form="♀ (female)"]  # not connected
  J37 = female pin header, 1 pin [form="♀ (female)"]  # not connected
  J38 = female pin header, 1 pin [form="♀ (female)"]  # not connected
  J39 = female pin header, 1 pin [form="♀ (female)"]  # not connected
  J40 = female pin header, 1 pin [form="♀ (female)"]  # not connected
  J41 = female pin header, 1 pin [form="♀ (female)"]  # not connected
  J42 = female pin header, 1 pin [form="♀ (female)"]  # not connected
  J43 = female pin header, 1 pin [form="♀ (female)"]  # not connected
  J44 = female pin header, 1 pin [form="♀ (female)"]  # not connected
  J45 = female pin header, 1 pin [form="♀ (female)"]  # not connected
  J46 = female pin header, 1 pin [form="♀ (female)"]  # not connected
  J47 = female pin header, 1 pin [form="♀ (female)"]  # not connected
  J48 = female pin header, 1 pin [form="♀ (female)"]  # not connected
  J49 = female pin header, 1 pin [form="♀ (female)"]  # not connected
  J50 = female pin header, 1 pin [form="♀ (female)"]  # not connected
  J51 = female pin header, 1 pin [form="♀ (female)"]  # not connected
  J52 = female pin header, 1 pin [form="♀ (female)"]  # not connected
  J53 = female pin header, 1 pin [form="♀ (female)"]  # not connected
  J54 = female pin header, 1 pin [form="♀ (female)"]  # not connected
  J55 = female pin header, 1 pin [form="♀ (female)"]  # not connected
  J56 = female pin header, 1 pin [form="♀ (female)"]  # not connected
  J57 = female pin header, 1 pin [form="♀ (female)"]  # not connected
  J58 = female pin header, 1 pin [form="♀ (female)"]  # not connected
  J59 = female pin header, 1 pin [form="♀ (female)"]  # not connected
  J60 = female pin header, 1 pin [form="♀ (female)"]  # not connected
  J61 = female pin header, 1 pin [form="♀ (female)"]  # not connected
  J62 = female pin header, 1 pin [form="♀ (female)"]  # not connected
  J63 = female pin header, 1 pin [form="♀ (female)"]  # not connected
  J64 = female pin header, 1 pin [form="♀ (female)"]  # not connected
  J65 = female pin header, 1 pin [form="♀ (female)"]  # not connected
  J66 = female pin header, 1 pin [form="♀ (female)"]  # not connected
  J67 = female pin header, 1 pin [form="♀ (female)"]  # not connected
  J68 = female pin header, 1 pin [form="♀ (female)"]
  J69 = female pin header, 1 pin [form="♀ (female)"]
  J70 = female pin header, 1 pin [form="♀ (female)"]
  J71 = female pin header, 1 pin [form="♀ (female)"]
  J72 = female pin header, 1 pin [form="♀ (female)"]
  J73 = female pin header, 1 pin [form="♀ (female)"]
  5V = female pin header, 7 pins [form="♀ (female)"]
  GND = female pin header, 7 pins [form="♀ (female)"]
  J74 = female pin header, 1 pin [form="♀ (female)"]
  J75 = female pin header, 1 pin [form="♀ (female)"]  # not connected
  J76 = female pin header, 1 pin [form="♀ (female)"]  # not connected
  J77 = female pin header, 1 pin [form="♀ (female)"]  # not connected
  J78 = female pin header, 1 pin [form="♀ (female)"]  # not connected
  J79 = female pin header, 1 pin [form="♀ (female)"]  # not connected
  J80 = female pin header, 1 pin [form="♀ (female)"]  # not connected
  J81 = female pin header, 1 pin [form="♀ (female)"]  # not connected
  J82 = female pin header, 1 pin [form="♀ (female)"]  # not connected
  J83 = female pin header, 1 pin [form="♀ (female)"]  # not connected
  J84 = female pin header, 1 pin [form="♀ (female)"]  # not connected
  J85 = female pin header, 1 pin [form="♀ (female)"]  # not connected
  HC-05_B/T = female pin header, 6 pins [form="♀ (female)"]
  SPI = female pin header, 3 pins [form="♀ (female)"]
  I2C = female pin header, 2 pins [form="♀ (female)"]
  SJ1 = Solder Jumper [package=sj_2s]
  U9 = DIODE-ZENER [part_number=MM3Z5V6ST1G package=sod-323]
  Pad1 = Pad [width=5.2000000000000002 height=5.2000000000000002 connect=center]
  MPX4250AP = MPX4250AP pressure sensor2 [part_number=MPX]
  R47 = Resistor [tolerance=±5% resistance=1k part_number=RC0805FR-071KL package="0805 [SMD]"]
  R48 = Resistor [tolerance=±5% resistance=2k package="0805 [SMD]"]
  Q1 = TRANSISTOR_PNP [part_number=ZXTP07040DFF package=sot23-3]
  C24 = Electrolytic Capacitor [capacitance=22µF voltage=16V part_number=EEE-FK0J220R package="0405 [SMD, electrolytic]"]
  C25 = Ceramic Capacitor [capacitance=0.1µF part_number=CL21F104ZBCNNNC package="0805 [SMD, multilayer]"]
  12v = female pin header, 2 pins [form="♀ (female)"]
  R49 = Resistor [tolerance=±5% resistance=2.2k package="0805 [SMD]"]
  S1 = SWITCH-DPDT [package=ayz0202]
  R50 = Resistor [tolerance=±1% resistance=120 package="0805 [SMD]"]
  IC8 = SO08 [chip_label=SO08 part_number=VNLD5090-E package=SO]
  R52 = Resistor [tolerance=±1% resistance=1k part_number=RC0805FR-071KL package="0805 [SMD]"]
  R53 = Resistor [tolerance=±1% resistance=1k part_number=RC0805FR-071KL package="0805 [SMD]"]
  R54 = Resistor [tolerance=±1% resistance=100k part_number=RC0805FR-071KL package="0805 [SMD]"]
  R55 = Resistor [tolerance=±1% resistance=100k part_number=RC0805FR-071KL package="0805 [SMD]"]
  Part37 = 174518_DENSO-ECU-socket_64pin-040-070 [part_number=174518 package="64-pin 0.40/0.70"]
  D7 = Rectifier Diode [part_number=1N4001 package="300 mil [THT]"]
  D8 = Rectifier Diode [part_number=1N4001 package="300 mil [THT]"]
  R56 = Resistor [tolerance=±5% resistance=2.2k package="0805 [SMD]"]  # not connected

nets (from the pcb view):
  N1: Arduino_Mega_2560.A8, IC6.12, J69.pin1
  N2: Arduino_Mega_2560.A9, IC7.36
  N3: Arduino_Mega_2560.A10, IC7.35
  N4: Arduino_Mega_2560.A0, IC6.1, R2.Pin_1, C2.1
  N5: Arduino_Mega_2560.A1, IC6.2, R4.Pin_1, C4.1
  N6: Arduino_Mega_2560.A2, IC6.3, C6.1, R5.Pin_1
  N7: Arduino_Mega_2560.A3, IC6.4, R9.Pin_1, C10.1
  N8: Arduino_Mega_2560.A4, IC6.5, R8.Pin_1, C8.1
  N9: Arduino_Mega_2560.A5, IC6.6, R38.Pin_1, C19.0
  N10: Arduino_Mega_2560.A6, IC7.10
  N11: Arduino_Mega_2560.D21/SCL, Arduino_Mega_2560.SCL, I2C.pin2
  N12: Arduino_Mega_2560.D20/SDA, Arduino_Mega_2560.SDA, I2C.pin1
  N13: Arduino_Mega_2560.D19/RX1, IC6.15, C23.0, R35.Pin_1
  N14: Arduino_Mega_2560.D18/TX1, IC6.14, C22.1, R34.Pin_1
  N15: Arduino_Mega_2560.D17_PWM/RX2, DRV8825_Stepper.STEP
  N16: Arduino_Mega_2560.D16_PWM/TX2, DRV8825_Stepper.DIR
  N17: Arduino_Mega_2560.D11_PWM, R14.Pin_0, R18.Pin_0
  N18: Arduino_Mega_2560.D10_PWM, R19.Pin_0, R15.Pin_0
  N19: Arduino_Mega_2560.D9_PWM, R20.Pin_0, R16.Pin_0
  N20: Arduino_Mega_2560.D8_PWM, R21.Pin_0, R17.Pin_0
  N21: Arduino_Mega_2560.RESET, C11.1, SJ1.2, S1.5
  N22: Arduino_Mega_2560.5V, IC7.17, IC1.6, C15.+, C13.1, IC6.16, U6.C, R39.Pin_0, D6.C, DRV8825_Stepper.RESET, DRV8825_Stepper.SLEEP, HC-05_B/T.pin2, U9.C, R49.Pin_0, R50.Pin_0
  N23: Arduino_Mega_2560.D0_RX0, HC-05_B/T.pin4
  N24: Arduino_Mega_2560.D1_TX0, R47.Pin_1
  N25: Arduino_Mega_2560.D2_PWM, R42.Pin_0
  N26: Arduino_Mega_2560.D3_PWM, IC6.13, J70.pin1, R49.Pin_1
  N27: Arduino_Mega_2560.D4_PWM, R40.Pin_0
  N28: Arduino_Mega_2560.D23, HC-05_B/T.pin1
  N29: Arduino_Mega_2560.D24, DRV8825_Stepper.ENABLE
  N30: Arduino_Mega_2560.D35, R52.Pin_0
  N31: Arduino_Mega_2560.D37, R46.Pin_1, U8.C
  N32: Arduino_Mega_2560.D39, R24.Pin_0
  N33: Arduino_Mega_2560.D41, R25.Pin_0
  N34: Arduino_Mega_2560.D44, J68.pin1
  N35: Arduino_Mega_2560.D46, J73.pin1
  N36: Arduino_Mega_2560.D49, R53.Pin_0
  N37: Arduino_Mega_2560.D50, IC7.16, SPI.pin2
  N38: Arduino_Mega_2560.D51, IC7.13, SPI.pin1
  N39: Arduino_Mega_2560.D52, IC7.12, SPI.pin3
  N40: D5.cathode, IC7.11, Q1.E
  N41: D5.anode, U2.P$1, IC7.37, R11.Pin_0, R10.Pin_0, C17.1, R12.Pin_0, R13.Pin_0, C18.+, R7.Pin_0, DRV8825_Stepper.VMOT, 12v.pin1, 12v.pin2, Part37.4B, D7.cathode, D8.cathode
  N42: U2.P$2, C17.0, C18.-, C8.0
  N43: IC7.14, Q1.B
  N44: IC7.15, IC7.22, IC7.38, IC7.40, IC7.42, Pad1.pad
  N45: IC7.18, Q1.C, C24.+, C25.1
  N46: IC7.19, SJ1.1
  N47: IC7.20, C14.1, C16.+, R3.Pin_0, R1.Pin_0, R37.Pin_0, R36.Pin_0, U7.C, C20.1, C21.1, 5V.pin1, 5V.pin2, 5V.pin3, 5V.pin4, 5V.pin5, 5V.pin6, 5V.pin7, MPX4250AP.Vs, Part37.3I
  N48: IC7.23, J72.pin1
  N49: IC7.41, J71.pin1
  N50: IC1.2, R31.Pin_1, R24.Pin_1
  N51: IC1.3, R30.Pin_0
  N52: IC1.4, R30.Pin_1, R25.Pin_1
  N53: IC1.5, R27.Pin_1, R44.Pin_0
  N54: IC1.7, R26.Pin_1, R45.Pin_1
  N55: IC4.1, R14.Pin_1
  N56: IC4.3, R15.Pin_1
  N57: IC4.6, D3.C, Part37.4W
  N58: IC4.8, D4.C, Part37.4U
  N59: R19.Pin_1, R18.Pin_1, R20.Pin_1, R21.Pin_1
  N60: R11.Pin_1, LED2.anode
  N61: R10.Pin_1, LED1.anode
  N62: LED2.cathode, D3.A
  N63: C15.-, C13.0
  N64: C14.0, C16.-
  N65: R16.Pin_1, IC3.1
  N66: R17.Pin_1, IC3.3
  N67: IC3.5, C23.1, C2.0, Part37.3O, Part37.4A, Part37.4C, Part37.4D
  N68: IC3.6, D1.C, Part37.4V
  N69: IC3.8, D2.C, Part37.4X
  N70: LED4.cathode, D1.A
  N71: LED4.anode, R13.Pin_1
  N72: R12.Pin_1, LED3.anode
  N73: LED3.cathode, D2.A
  N74: C3.1, R3.Pin_1, R4.Pin_0, Part37.3G
  N75: C1.1, R1.Pin_1, R2.Pin_0, Part37.3K
  N76: C7.1, R8.Pin_0, R7.Pin_1, R6.Pin_0
  N77: C5.1, R5.Pin_0, Part37.3F
  N78: C9.1, R9.Pin_0, Part37.3C
  N79: D4.A, LED1.cathode
  N80: R37.Pin_1, R35.Pin_0, Part37.4F
  N81: LED5.cathode, LED6.cathode
  N82: LED5.anode, R26.Pin_0
  N83: LED6.anode, R27.Pin_0
  N84: R34.Pin_0, R36.Pin_1, Part37.4G
  N85: R39.Pin_1, D6.A, S1.4
  N86: R44.Pin_1, Part37.4R
  N87: R45.Pin_0, Part37.4N
  N88: R46.Pin_0, Part37.1L
  N89: R38.Pin_0, MPX4250AP.V_out
  N90: C19.1, C20.0
  N91: IC5.1, R43.Pin_1, R42.Pin_1
  N92: IC5.3, R40.Pin_1, R41.Pin_1
  N93: IC5.5, R41.Pin_0
  N94: IC5.6, J74.pin1, D8.anode
  N95: IC5.8, Part37.4Q, D7.anode
  N96: GND.pin1, GND.pin2, GND.pin3, GND.pin4, GND.pin5, GND.pin6, GND.pin7
  N97: HC-05_B/T.pin5, R47.Pin_0, R48.Pin_1
  N98: S1.6, R50.Pin_1
  N99: IC8.1, R52.Pin_1, R54.Pin_0
  N100: IC8.3, R53.Pin_1, R55.Pin_1
  N101: IC8.6, Part37.1U
  N102: IC8.7, Part37.1O
  N103: IC8.8, Part37.1A
  N104: R54.Pin_1, R55.Pin_0

notes:
  Speeduino Pro, Inlet Air Temperature sensor
  Coolant Temperature Sensor
  Speeduino Pro, Throttle Position Sensor
  Battery Reference Voltage
  Speeduino Pro v1, Injectors
  Speeduino v0.4, O2 Sensor
  Ignitor output 1
  Power supply
  Crank and Cam sensors
  Speeduino Pro, MAP sensor input
  PWM Idle / Boost
  inj1
  Reset Protection - Refer AVR040 Application note
  ADC Clamping circuit
  Stepper Driver
  TAPR 1.0
  © Josh Stewart
  Arduino Mega 2560
  MC33814
  2A
  1A
  Proto Area
  Clutch input
  Boost
  A8
  Flex
  Bluetooth Connector
  5V
  GND
  RX
  TX
  D20
  D21
  D44
  D48
  D46
  48-Pin Connector
  MX5 NA8 PNP Beta 1
  Run
  Prog
  F/P
  IGN2
  IGN1
  Flex Sensor input
  Fan and fuel pump outputs
  Flat side up
  Potential case: 1455Q1602
  64-pin Connector
  Speeduino
  VSS input

custom parts:
  MPX4250AP pressure sensor2: MPX4250AP - MPX4250A SERIES Motorola Preferred Device ORIGINAL MANUFACTURER MOUNTING - flat side up Integrated Silicon Pressure Sensor Manifold Absolute Pressure Sensor On-Chip Signal Conditioned, Temperature Compensated and Calibrated The MPX4250A series piezoresistive transducer is a state-of-the-art monolithic silicon pressure sensor designed for a wide range of applications, particularly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
