# Fritzing sketch Teensy 3.5 Adaptor (saved by Fritzing 0.9.3b)
circuit board: 10.16cm x 5.30577cm
breadboards: 1

parts:
  J1 = female pin header, 24 pins [form="♀ (female)"]
  J2 = female pin header, 24 pins [form="♀ (female)"]
  J3 = female pin header, 5 pins [form="♀ (female)"]
  Part1 = Arduino Mega 2560 (Rev3)
  IC1 = LMV324 [part_number=LMV324LIDT package=so014]
  R1 = Resistor [tolerance=±0.1% resistance=180k part_number=TNPW0805180KBEEA package="0805 [SMD]"]
  R2 = Resistor [tolerance=±0.1% resistance=330k part_number=RT0805BRD07330KL package="0805 [SMD]"]
  R3 = Resistor [tolerance=±0.1% resistance=180k part_number=TNPW0805180KBEEA package="0805 [SMD]"]
  R4 = Resistor [tolerance=±0.1% resistance=330k part_number=RT0805BRD07330KL package="0805 [SMD]"]
  R5 = Resistor [tolerance=±0.1% resistance=180k part_number=TNPW0805180KBEEA package="0805 [SMD]"]
  R6 = Resistor [tolerance=±0.1% resistance=330k part_number=RT0805BRD07330KL package="0805 [SMD]"]
  R7 = Resistor [tolerance=±0.1% resistance=180k part_number=TNPW0805180KBEEA package="0805 [SMD]"]
  R8 = Resistor [tolerance=±0.1% resistance=330k part_number=RT0805BRD07330KL package="0805 [SMD]"]
  IC2 = LMV324 [part_number=LMV324LIDT package=so014]
  R9 = Resistor [tolerance=±0.1% resistance=330k part_number=RT0805BRD07330KL package="0805 [SMD]"]
  R10 = Resistor [tolerance=±0.1% resistance=180k part_number=TNPW0805180KBEEA package="0805 [SMD]"]
  R11 = Resistor [tolerance=±0.1% resistance=330k part_number=RT0805BRD07330KL package="0805 [SMD]"]
  R12 = Resistor [tolerance=±0.1% resistance=180k part_number=TNPW0805180KBEEA package="0805 [SMD]"]
  R13 = Resistor [tolerance=±0.1% resistance=330k part_number=RT0805BRD07330KL package="0805 [SMD]"]
  R14 = Resistor [tolerance=±0.1% resistance=180k part_number=TNPW0805180KBEEA package="0805 [SMD]"]
  R15 = Resistor [tolerance=±0.1% resistance=330k part_number=RT0805BRD07330KL package="0805 [SMD]"]
  R16 = Resistor [tolerance=±0.1% resistance=180k part_number=TNPW0805180KBEEA package="0805 [SMD]"]

nets:
  GND: J1.pin1, J2.pin10, J3.pin3, Part1.GND, IC1.G$1_-V, R2.Pin_0, R4.Pin_0, R6.Pin_0, R8.Pin_0, IC2.G$1_-V, R9.Pin_0, R11.Pin_0, R13.Pin_0, R15.Pin_0
  D0: J1.pin2, Part1.D0_RX0
  D1: J1.pin3, Part1.D1_TX0
  D2: J1.pin4, Part1.D2_PWM
  D3: J1.pin5, Part1.D3_PWM
  D4: J1.pin6, Part1.D4_PWM
  D5: J1.pin7, Part1.D5_PWM
  D6: J1.pin8, Part1.D6_PWM
  D7: J1.pin9, Part1.D7_PWM
  D8: J1.pin10, Part1.D8_PWM
  D9: J1.pin11, Part1.D9_PWM
  D10: J1.pin12, Part1.D10_PWM
  D11: J1.pin13, Part1.D11_PWM
  D12: J1.pin14, Part1.D12_PWM
  3V3: J1.pin15, J2.pin22, IC1.G$1_+V, IC2.G$1_+V
  D24-T/D41-A: J1.pin16, Part1.D41
  D25-T/D42-A: J1.pin17, Part1.D42
  D26-T/D43-A: J1.pin18, Part1.D43
  D27-T/D47-A: J1.pin19, Part1.D47
  D28-T/D49-A: J1.pin20, Part1.D49
  D29-T/D50-A: J1.pin21, Part1.D50
  D30-T/D52-A: J1.pin22, Part1.D52
  D31-T/D40-A: J1.pin23, Part1.D40
  D32-T/D39-A: J1.pin24, Part1.D39
  D16-A/D33-T: J2.pin1, Part1.D16_PWM/TX2
  D17: J2.pin2, Part1.D17_PWM/RX2
  D18: J2.pin3, Part1.D18/TX1
  D24-A/D38-T: J2.pin6, Part1.D24
  D36-A/D39-T: J2.pin7, Part1.D36
  A0-3V3: J2.pin12, IC1.G$1_OUT, IC1.G$1_-IN
  A1-3V3: J2.pin13, IC1.G$2_-IN, IC1.G$2_OUT
  A2-3V3: J2.pin14, IC1.G$4_-IN, IC1.G$4_OUT
  A3-3V3: J2.pin15, IC1.G$3_OUT, IC1.G$3_-IN
  A4-3V3: J2.pin16, IC2.G$1_OUT, IC2.G$1_-IN
  A5-3V3: J2.pin17, IC2.G$2_-IN, IC2.G$2_OUT
  A6-3V3: J2.pin18, IC2.G$4_-IN, IC2.G$4_OUT
  A7-3V3: J2.pin19, IC2.G$3_OUT, IC2.G$3_-IN
  D22-T/D26-A: J2.pin20, Part1.D26
  D19-A/D23-T: J2.pin21, Part1.D19/RX1
  5V: J2.pin24, Part1.5V
  A8-5V: Part1.A8
  A0-5V: Part1.A0, R3.Pin_1
  A1-5V: Part1.A1, R1.Pin_1
  A2-5V: Part1.A2, R5.Pin_1
  A3-5V: Part1.A3, R7.Pin_1
  A4-5V: Part1.A4, R14.Pin_1
  A5-5V: Part1.A5, R16.Pin_1
  A6-5V: Part1.A6, R12.Pin_1
  A7-5V: Part1.A7, R10.Pin_1
  D15: Part1.D15/RX3
  D14: Part1.D14/TX3
  D21: Part1.SCL
  D20: Part1.SDA
  D22: Part1.D22
  D23: Part1.D23
  N1: IC1.G$1_+IN, R3.Pin_0, R4.Pin_1
  N2: IC1.G$2_+IN, R1.Pin_0, R2.Pin_1
  N3: IC1.G$3_+IN, R7.Pin_0, R8.Pin_1
  N4: IC1.G$4_+IN, R5.Pin_0, R6.Pin_1
  N5: IC2.G$1_+IN, R13.Pin_1, R14.Pin_0
  N6: IC2.G$2_+IN, R15.Pin_1, R16.Pin_0
  N7: IC2.G$3_+IN, R9.Pin_1, R10.Pin_0
  N8: IC2.G$4_+IN, R11.Pin_1, R12.Pin_0

notes:
  Speeduino Teensy Adapter, Op AMP 1
  Speeduino Teensy Adapter, Op AMP 2
  Pin Translation
  © Josh Stewart
  TAPR 1.0
  Speeduino To Teensy 3.5
  PVT1
  Teensy 3.5
  Arduino 2560
