# Fritzing sketch VR Conditioner v3.1 (saved by Fritzing 0.9.3b)
circuit board: 2.89999cm x 2.89999cm
breadboards: 1

parts:
  IC1 = IC, DIP package, 8 pins [chip_label=IC]
  R10 = Resistor [tolerance=±5% resistance=4.7k power=3W package=THT]
  R12 = Resistor [tolerance=±5% resistance=4.7k power=3W package=THT]
  C3 = Ceramic Capacitor [capacitance=1µF package="0805 [SMD, multilayer]"]
  C2 = Ceramic Capacitor [capacitance=0.01µF package="0805 [SMD, multilayer]"]
  C1 = Ceramic Capacitor [capacitance=0.1µF package="0805 [SMD, multilayer]"]
  MAX9926 = QSOP16 [chip_label="HT SSOP28" package=QSOP16]
  R6 = Resistor [tolerance=±1% resistance=1k package="0805 [SMD]"]
  R4 = Resistor [tolerance=±1% resistance=1k package="0805 [SMD]"]
  R9 = Resistor [tolerance=±5% resistance=10k package="0805 [SMD]"]
  R7 = Resistor [tolerance=±5% resistance=10k package="0805 [SMD]"]
  C4 = Ceramic Capacitor [capacitance=1nF package="0805 [SMD, multilayer]"]
  R13 = Resistor [tolerance=±5% resistance=10k package="0805 [SMD]"]
  C5 = Ceramic Capacitor [capacitance=1nF package="0805 [SMD, multilayer]"]
  R11 = Resistor [tolerance=±5% resistance=10k package="0805 [SMD]"]
  J1 = female pin header, 2 pins [form="♀ (female)"]

nets:
  VR1-: IC1.pin1, R10.Pin_1, R9.Pin_1
  VR1+: IC1.pin2, R10.Pin_0, R7.Pin_1
  VR2+: IC1.pin3, R12.Pin_0, R13.Pin_1
  VR2-: IC1.pin4, R12.Pin_1, R11.Pin_1
  5V: IC1.pin5, C3.1, C2.1, C1.1, MAX9926.14, R6.Pin_0, R4.Pin_0
  GND: IC1.pin6, C3.0, C2.0, C1.0, MAX9926.1, MAX9926.3, MAX9926.6, MAX9926.8, MAX9926.11, MAX9926.13
  Output2: IC1.pin7, MAX9926.5, R6.Pin_1, J1.pin1
  Output1: IC1.pin8, MAX9926.4, R4.Pin_1, J1.pin2
  N1: MAX9926.9, R13.Pin_0, C5.1
  N2: MAX9926.10, C5.0, R11.Pin_0
  N3: MAX9926.15, R9.Pin_0, C4.0
  N4: MAX9926.16, R7.Pin_0, C4.1

notes:
  I/O Connector
  VR Conditioner - Operating mode A2
  Bottom
  Top
  Dual VR Conditioner v3.1
  © Josh Stewart
  5v
  GND
  Out2
  Out1
