# Fritzing sketch schematic v0.2 (saved by Fritzing 0.8.7b)
circuit board: 10cm x 13.8143cm
breadboards: 1

parts:
  Arduino_Mega_2560 = Arduino Mega 2560 (Rev3) [part_number="Arduino Mega 2560"]
  R1 = Resistor [tolerance=±5% resistance=2.49k package=THT]
  R2 = Resistor [tolerance=±5% resistance=470 package=THT]
  D1 = Schottky Diode [part_number=1N5818 package="300 mil [THT]"]
  D2 = Schottky Diode [part_number=1N5818 package="300 mil [THT]"]
  R3 = Resistor [tolerance=±5% resistance=2.49k package=THT]
  R4 = Resistor [tolerance=±5% resistance=470 package=THT]
  D3 = Schottky Diode [part_number=1N5818 package="300 mil [THT]"]
  D4 = Schottky Diode [part_number=1N5818 package="300 mil [THT]"]
  J1 = screw terminal, 7 pins
  R6 = Resistor [tolerance=±5% resistance=470 package=THT]
  D5 = Schottky Diode [part_number=1N5818 package="300 mil [THT]"]
  D6 = Schottky Diode [part_number=1N5818 package="300 mil [THT]"]
  R7 = Resistor [tolerance=±5% resistance=3.9k package=THT]
  R8 = Resistor [tolerance=±5% resistance=470 package=THT]
  D8 = Schottky Diode [part_number=1N5818 package="300 mil [THT]"]
  D7 = Schottky Diode [part_number=1N5818 package="300 mil [THT]"]
  R9 = Resistor [tolerance=±5% resistance=2.2k package=THT]
  LED1 = LED - 5mm [color="Red (633nm)" package="5 mm [THT]"]
  D9 = Rectifier Diode [part_number=1N4004 package="300 mil [THT]"]
  Q1 = Basic FET N-Channel [part_number=VND7NV04 package="TO220 [THT]"]
  R10 = Resistor [tolerance=±5% resistance=1k package=THT]
  R11 = Resistor [tolerance=±5% resistance=100k package=THT]
  J2 = screw terminal, 4 pins
  C7 = Ceramic Capacitor [capacitance=0.1µF package="200 mil [THT, multilayer]"]
  C1 = Ceramic Capacitor [capacitance=0.1µF package="200 mil [THT, multilayer]"]
  C3 = Ceramic Capacitor [capacitance=0.1µF package="200 mil [THT, multilayer]"]
  C5 = Ceramic Capacitor [capacitance=0.1µF package="200 mil [THT, multilayer]"]
  J3 = screw terminal, 2 pins
  R12 = Resistor [tolerance=±5% resistance=2.2k package=THT]
  LED3 = LED - 5mm [color="Red (633nm)" package="5 mm [THT]"]
  D10 = Rectifier Diode [part_number=1N4004 package="300 mil [THT]"]
  Q2 = Basic FET N-Channel [part_number=VND7NV04 package="TO220 [THT]"]
  R13 = Resistor [tolerance=±5% resistance=1k package=THT]
  R14 = Resistor [tolerance=±5% resistance=100k package=THT]
  R15 = Resistor [tolerance=±5% resistance=2.2k package=THT]
  LED2 = LED - 5mm [color="Red (633nm)" package="5 mm [THT]"]
  D11 = Rectifier Diode [part_number=1N4004 package="300 mil [THT]"]
  Q3 = Basic FET N-Channel [part_number=VND7NV04 package="TO220 [THT]"]
  R16 = Resistor [tolerance=±5% resistance=1k package=THT]
  R17 = Resistor [tolerance=±5% resistance=100k package=THT]
  R18 = Resistor [tolerance=±5% resistance=2.2k package=THT]
  LED4 = LED - 5mm [color="Red (633nm)" package="5 mm [THT]"]
  D12 = Rectifier Diode [part_number=1N4004 package="300 mil [THT]"]
  Q4 = Basic FET N-Channel [part_number=VND7NV04 package="TO220 [THT]"]
  R19 = Resistor [tolerance=±5% resistance=1k package=THT]
  R20 = Resistor [tolerance=±5% resistance=100k package=THT]
  C2 = Ceramic Capacitor [capacitance=0.22µF package="200 mil [THT, multilayer]"]
  C8 = Ceramic Capacitor [capacitance=0.22µF package="200 mil [THT, multilayer]"]
  R21 = Resistor [tolerance=±5% resistance=1k package=THT]
  C9 = Ceramic Capacitor [capacitance=0.1µF package="200 mil [THT, multilayer]"]
  R22 = Resistor [tolerance=±5% resistance=470 package=THT]
  D13 = Schottky Diode [part_number=1N5818 package="300 mil [THT]"]
  C6 = Ceramic Capacitor [capacitance=0.22µF package="200 mil [THT, multilayer]"]
  C4 = Ceramic Capacitor [capacitance=0.22µF package="200 mil [THT, multilayer]"]
  C10 = Ceramic Capacitor [capacitance=0.22µF package="200 mil [THT, multilayer]"]
  D14 = Schottky Diode [part_number=1N5818 package="300 mil [THT]"]
  IC1 = IC, DIP package, 8 pins [chip_label=IC part_number=TC4424EPA]
  R23 = Resistor [tolerance=±5% resistance=1k package=THT]
  R24 = Resistor [tolerance=±5% resistance=1k package=THT]
  JP1 = Header 3 [package=screwterminal-3.5mm-3_lock.007s]
  C11 = Ceramic Capacitor [capacitance=1µF package="200 mil [THT, multilayer]"]
  R25 = Resistor [tolerance=±5% resistance=150 package=THT]
  R26 = Resistor [tolerance=±5% resistance=2.2k package=THT]
  LED5 = LED - 5mm [color="Red (633nm)" package="5 mm [THT]"]
  J4 = screw terminal, 4 pins
  R27 = Resistor [tolerance=±5% resistance=150 package=THT]
  R28 = Resistor [tolerance=±5% resistance=2.2k package=THT]
  LED6 = LED - 5mm [color="Red (633nm)" package="5 mm [THT]"]
  IC2 = IC, DIP package, 8 pins [chip_label=IC part_number=TC4424EPA]
  R29 = Resistor [tolerance=±5% resistance=1k package=THT]
  R30 = Resistor [tolerance=±5% resistance=1k package=THT]
  C12 = Ceramic Capacitor [capacitance=1µF package="200 mil [THT, multilayer]"]
  R31 = Resistor [tolerance=±5% resistance=150 package=THT]
  R32 = Resistor [tolerance=±5% resistance=150 package=THT]
  R33 = Resistor [tolerance=±5% resistance=2.2k package=THT]
  R34 = Resistor [tolerance=±5% resistance=2.2k package=THT]
  LED7 = LED - 5mm [color="Red (633nm)" package="5 mm [THT]"]
  LED8 = LED - 5mm [color="Red (633nm)" package="5 mm [THT]"]
  U1 = Voltage Regulator - 5V [package="TO220 [THT]"]
  D15 = Schottky Diode [part_number=1N5818 package="300 mil [THT]"]
  U2 = V18ZA2P [package=v18za2p]
  C14 = Tantalum Capacitor [capacitance=47µF voltage=10V package="200 mil [THT, tantalum]"]
  C13 = Ceramic Capacitor [capacitance=0.1µF voltage=50V package="200 mil [THT, multilayer]"]
  C15 = Ceramic Capacitor [capacitance=0.1µF voltage=50V package="200 mil [THT, multilayer]"]
  C16 = Tantalum Capacitor [capacitance=10µF voltage=35V package="200 mil [THT, tantalum]"]

nets (from the pcb view):
  N1: Arduino_Mega_2560.A8, R22.Pin_1, D13.cathode, C10.1, D14.anode
  N2: Arduino_Mega_2560.A0, R2.Pin_1, D1.anode, D2.cathode, C2.1
  N3: Arduino_Mega_2560.A1, R4.Pin_1, D3.anode, D4.cathode, C4.1
  N4: Arduino_Mega_2560.A2, R6.Pin_1, D5.anode, D6.cathode, C6.1
  N5: Arduino_Mega_2560.A3, R8.Pin_1, D8.cathode, D7.anode, C8.1
  N6: Arduino_Mega_2560.D11_PWM, R19.Pin_0, R20.Pin_0
  N7: Arduino_Mega_2560.D10_PWM, R13.Pin_0, R14.Pin_0
  N8: Arduino_Mega_2560.D9_PWM, R16.Pin_0, R17.Pin_0
  N9: Arduino_Mega_2560.D8_PWM, R10.Pin_0, R11.Pin_0
  N10: Arduino_Mega_2560.5V, R1.Pin_0, D1.cathode, R3.Pin_0, D3.cathode, J1.pin2, J1.pin4, J1.pin6, D5.cathode, D7.cathode, D14.cathode, JP1.1, U1.output_voltage, C14.+, C13.1
  N11: Arduino_Mega_2560.D24, R24.Pin_0
  N12: Arduino_Mega_2560.D28, R23.Pin_0
  N13: Arduino_Mega_2560.D36, R30.Pin_0
  N14: Arduino_Mega_2560.D40, R29.Pin_0
  N15: R1.Pin_1, R2.Pin_0, J1.pin7, C1.1
  N16: R3.Pin_1, R4.Pin_0, J1.pin5, C3.1
  N17: J1.pin3, R6.Pin_0, C5.1
  N18: R7.Pin_0, R9.Pin_0, R12.Pin_0, R15.Pin_0, R18.Pin_0, JP1.3, U1.input_voltage, D15.cathode, C15.1, C16.+
  N19: R7.Pin_1, R8.Pin_0, C7.1, R21.Pin_0
  N20: R9.Pin_1, LED1.anode
  N21: LED1.cathode, D9.anode
  N22: D9.cathode, Q1.drain, J2.pin4
  N23: Q1.gate, R10.Pin_1
  N24: J2.pin1, D12.cathode, Q4.drain
  N25: J2.pin2, D10.cathode, Q2.drain
  N26: J2.pin3, D11.cathode, Q3.drain
  N27: J3.pin2, D15.anode, U2.P$1
  N28: R12.Pin_1, LED3.anode
  N29: LED3.cathode, D10.anode
  N30: Q2.gate, R13.Pin_1
  N31: R15.Pin_1, LED2.anode
  N32: LED2.cathode, D11.anode
  N33: Q3.gate, R16.Pin_1
  N34: R18.Pin_1, LED4.anode
  N35: LED4.cathode, D12.anode
  N36: Q4.gate, R19.Pin_1
  N37: C9.1, R22.Pin_0
  N38: IC1.pin2, R23.Pin_1
  N39: IC1.pin4, R24.Pin_1
  N40: IC1.pin5, R25.Pin_0
  N41: IC1.pin6, JP1.2, C11.1, IC2.pin6, C12.1
  N42: IC1.pin7, R27.Pin_1
  N43: R25.Pin_1, R26.Pin_1, J4.pin3
  N44: R26.Pin_0, LED5.anode
  N45: J4.pin1, R32.Pin_1, R34.Pin_1
  N46: J4.pin2, R31.Pin_0, R33.Pin_1
  N47: J4.pin4, R27.Pin_0, R28.Pin_1
  N48: R28.Pin_0, LED6.anode
  N49: IC2.pin2, R29.Pin_1
  N50: IC2.pin4, R30.Pin_1
  N51: IC2.pin5, R32.Pin_0
  N52: IC2.pin7, R31.Pin_1
  N53: R33.Pin_0, LED7.anode
  N54: R34.Pin_0, LED8.anode

notes:
  Inlet Air Temperature sensor
  Coolant Temperature Sensor
  Speeduino v0.2, Throttle Position Sensor
  Battery Reference Voltage
  Injector 1
  Sensor Screw connector 1
  Injector 3
  Injector 2
  Injector 4
  Speeduino v0.2, O2 Sensor
  Ignitor output 1
  Ignitor output 2
  12v
  5v
  Power supply
