# Fritzing sketch NA Miata 48 pin (saved by Fritzing 0.9.2b)
circuit board: 4cm x 10cm
breadboards: 1

parts:
  J1 = shrouded pin header, 40 pins [form="♂ (shrouded male)"]
  1B = female pin header, 1 pin [form="♀ (female)"]
  1A = female pin header, 1 pin [form="♀ (female)"]  # not connected
  1D = female pin header, 1 pin [form="♀ (female)"]  # not connected
  1C = female pin header, 1 pin [form="♀ (female)"]  # not connected
  1F = female pin header, 1 pin [form="♀ (female)"]  # not connected
  1E = female pin header, 1 pin [form="♀ (female)"]  # not connected
  1H = female pin header, 1 pin [form="♀ (female)"]
  1G = female pin header, 1 pin [form="♀ (female)"]
  1J = female pin header, 1 pin [form="♀ (female)"]  # not connected
  1I = female pin header, 1 pin [form="♀ (female)"]  # not connected
  1L = female pin header, 1 pin [form="♀ (female)"]  # not connected
  1K = female pin header, 1 pin [form="♀ (female)"]  # not connected
  1N = female pin header, 1 pin [form="♀ (female)"]  # not connected
  1M = female pin header, 1 pin [form="♀ (female)"]  # not connected
  1P = female pin header, 1 pin [form="♀ (female)"]  # not connected
  1O = female pin header, 1 pin [form="♀ (female)"]  # not connected
  1R = female pin header, 1 pin [form="♀ (female)"]  # not connected
  1Q = female pin header, 1 pin [form="♀ (female)"]  # not connected
  1T = female pin header, 1 pin [form="♀ (female)"]  # not connected
  1S = female pin header, 1 pin [form="♀ (female)"]  # not connected
  1V = female pin header, 1 pin [form="♀ (female)"]
  1U = female pin header, 1 pin [form="♀ (female)"]  # not connected
  2A = female pin header, 1 pin [form="♀ (female)"]
  2B = female pin header, 1 pin [form="♀ (female)"]
  2D = female pin header, 1 pin [form="♀ (female)"]
  2C = female pin header, 1 pin [form="♀ (female)"]
  2E = female pin header, 1 pin [form="♀ (female)"]
  2F = female pin header, 1 pin [form="♀ (female)"]  # not connected
  2G = female pin header, 1 pin [form="♀ (female)"]
  2H = female pin header, 1 pin [form="♀ (female)"]  # not connected
  2I = female pin header, 1 pin [form="♀ (female)"]  # not connected
  2J = female pin header, 1 pin [form="♀ (female)"]  # not connected
  2K = female pin header, 1 pin [form="♀ (female)"]  # not connected
  2L = female pin header, 1 pin [form="♀ (female)"]
  2M = female pin header, 1 pin [form="♀ (female)"]  # not connected
  2N = female pin header, 1 pin [form="♀ (female)"]
  2O = female pin header, 1 pin [form="♀ (female)"]  # not connected
  2P = female pin header, 1 pin [form="♀ (female)"]
  2Q = female pin header, 1 pin [form="♀ (female)"]
  2R = female pin header, 1 pin [form="♀ (female)"]  # not connected
  2S = female pin header, 1 pin [form="♀ (female)"]  # not connected
  2T = female pin header, 1 pin [form="♀ (female)"]  # not connected
  2U = female pin header, 1 pin [form="♀ (female)"]
  2V = female pin header, 1 pin [form="♀ (female)"]
  2W = female pin header, 1 pin [form="♀ (female)"]
  2X = female pin header, 1 pin [form="♀ (female)"]  # not connected
  2Y = female pin header, 1 pin [form="♀ (female)"]
  2Z = female pin header, 1 pin [form="♀ (female)"]
  R1 = Resistor [tolerance=±5% resistance=20k package=THT]
  R2 = Resistor [tolerance=±5% resistance=10k package=THT]
  D1 = Zener Diode [part_number=1N4732A breakdown_voltage=5.1V package="300 mil [THT]"]
  J2 = screw terminal, 4 pins
  J3 = screw terminal, 2 pins

nets:
  INJ1: J1.pin1, J1.pin40, 2U.pin1
  INJ2: J1.pin2, J1.pin39, 2V.pin1
  INJ3: J1.pin3, J1.pin4, 2Y.pin1
  INJ4: J1.pin5, J1.pin6, 2Z.pin1
  IGN1: J1.pin7, 1G.pin1
  GND: J1.pin9, J1.pin10, J1.pin12, J1.pin23, 2A.pin1, 2B.pin1, 2D.pin1, 2C.pin1, R2.Pin_0, D1.anode, J3.pin1
  Clutch-in: J1.pin14, R1.Pin_1, R2.Pin_1, D1.cathode
  Coolant: J1.pin19, 2Q.pin1
  IAT: J1.pin20, 2P.pin1, J2.pin2
  O2: J1.pin21, 2N.pin1, J2.pin4
  TPS: J1.pin22, 2L.pin1, J2.pin3
  Cam: J1.pin24, 2G.pin1
  Crank: J1.pin25, 2E.pin1
  5V: J1.pin28, J2.pin1
  IGN2: J1.pin34, 1H.pin1
  Idle: J1.pin37, 2W.pin1
  12V: 1B.pin1, J3.pin2
  Clutch: 1V.pin1, R1.Pin_0

notes:
  1A
  2A
  5V
  GND
  48-pin OEM ECU Connector
  12V Clutch to 5V
  12V
  IAT
  O2
  TPS
  Speeduino - NA6 Miata for v0.4
  rev B
