# Fritzing sketch schematic v0.4.1 (saved by Fritzing 0.9.2b)
circuit board: 10cm x 10cm
breadboards: 1

parts:
  Arduino_Mega_2560 = Arduino Mega 2560 (Rev3) [part_number="Arduino Mega 2560"]
  R1 = Resistor [tolerance=±0.1% resistance=2.49k part_number=RC55Y-2K49BI package=THT]
  R2 = Resistor [tolerance=±5% resistance=470 package=THT]
  D1 = Schottky Diode [part_number=1N5818 package="300 mil [THT]"]
  D2 = Schottky Diode [part_number=1N5818 package="300 mil [THT]"]
  R3 = Resistor [tolerance=±0.1% resistance=2.49k part_number=RC55Y-2K49BI package=THT]
  R4 = Resistor [tolerance=±5% resistance=470 package=THT]
  D3 = Schottky Diode [part_number=1N5818 package="300 mil [THT]"]
  D4 = Schottky Diode [part_number=1N5818 package="300 mil [THT]"]
  R6 = Resistor [tolerance=±5% resistance=470 package=THT]
  D5 = Schottky Diode [part_number=1N5818 package="300 mil [THT]"]
  D6 = Schottky Diode [part_number=1N5818 package="300 mil [THT]"]
  R7 = Resistor [tolerance=±0.1% resistance=3.9k package=THT]
  R8 = Resistor [tolerance=±5% resistance=470 package=THT]
  D8 = Schottky Diode [part_number=1N5818 package="300 mil [THT]"]
  D7 = Schottky Diode [part_number=1N5818 package="300 mil [THT]"]
  R9 = Resistor [tolerance=±5% resistance=2.4k package=THT]
  D9 = Rectifier Diode [part_number=1N4004 package="300 mil [THT]"]
  Q1 = Basic FET N-Channel [part_number=STP62NS04Z package="TO220 [THT]"]
  R10 = Resistor [tolerance=±5% resistance=1k package=THT]
  R11 = Resistor [tolerance=±5% resistance=100k package=THT]
  C7 = Ceramic Capacitor [capacitance=0.1µF package="200 mil [THT, multilayer]"]
  C1 = Ceramic Capacitor [capacitance=0.1µF package="200 mil [THT, multilayer]"]
  C3 = Ceramic Capacitor [capacitance=0.1µF package="200 mil [THT, multilayer]"]
  C5 = Ceramic Capacitor [capacitance=0.1µF package="200 mil [THT, multilayer]"]
  J3 = screw terminal, 2 pins
  R15 = Resistor [tolerance=±5% resistance=2.4k package=THT]
  D11 = Rectifier Diode [part_number=1N4004 package="300 mil [THT]"]
  Q2 = Basic FET N-Channel [part_number=STP62NS04Z package="TO220 [THT]"]
  R16 = Resistor [tolerance=±5% resistance=1k package=THT]
  R17 = Resistor [tolerance=±5% resistance=100k package=THT]
  D10 = Rectifier Diode [part_number=1N4004 package="300 mil [THT]"]
  Q3 = Basic FET N-Channel [part_number=STP62NS04Z package="TO220 [THT]"]
  R13 = Resistor [tolerance=±5% resistance=1k power=0.25W package=THT]
  R14 = Resistor [tolerance=±5% resistance=100k power=0.25W package=THT]
  R18 = Resistor [tolerance=±5% resistance=2.4k package=THT]
  D12 = Rectifier Diode [part_number=1N4004 package="300 mil [THT]"]
  Q4 = Basic FET N-Channel [part_number=VND7NV04 package="TO220 [THT]"]
  R19 = Resistor [tolerance=±5% resistance=1k package=THT]
  R20 = Resistor [tolerance=±5% resistance=100k package=THT]
  C2 = Ceramic Capacitor [capacitance=0.22µF package="200 mil [THT, multilayer]"]
  C8 = Ceramic Capacitor [capacitance=0.22µF package="200 mil [THT, multilayer]"]
  R21 = Resistor [tolerance=±5% resistance=1k package=THT]
  C9 = Ceramic Capacitor [capacitance=0.1µF package="200 mil [THT, multilayer]"]
  R22 = Resistor [tolerance=±5% resistance=470 package=THT]
  D13 = Schottky Diode [part_number=1N5818 package="300 mil [THT]"]
  C6 = Ceramic Capacitor [capacitance=0.22µF package="200 mil [THT, multilayer]"]
  C4 = Ceramic Capacitor [capacitance=0.22µF package="200 mil [THT, multilayer]"]
  C10 = Ceramic Capacitor [capacitance=0.22µF package="200 mil [THT, multilayer]"]
  D14 = Schottky Diode [part_number=1N5818 package="300 mil [THT]"]
  IC1 = IC, DIP package, 8 pins [chip_label=IC part_number=TC4424EPA]
  R23 = Resistor [tolerance=±5% resistance=1k package=THT]
  R24 = Resistor [tolerance=±5% resistance=1k package=THT]
  C11 = Ceramic Capacitor [capacitance=1µF package="200 mil [THT, multilayer]"]
  R25 = Resistor [tolerance=±5% resistance=160 power=2W package=THT]
  R26 = Resistor [tolerance=±5% resistance=2.4k package=THT]
  R27 = Resistor [tolerance=±5% resistance=160 power=2W package=THT]
  R28 = Resistor [tolerance=±5% resistance=2.4k package=THT]
  IC2 = IC, DIP package, 8 pins [chip_label=IC part_number=TC4424EPA]
  R29 = Resistor [tolerance=±5% resistance=1k package=THT]
  R30 = Resistor [tolerance=±5% resistance=1k package=THT]
  C12 = Ceramic Capacitor [capacitance=1µF package="200 mil [THT, multilayer]"]
  R31 = Resistor [tolerance=±5% resistance=160 power=2W package=THT]
  R33 = Resistor [tolerance=±5% resistance=2.4k power=0.25W package=THT]
  R34 = Resistor [tolerance=±5% resistance=2.4k package=THT]
  U1 = Voltage Regulator - 5V [part_number=LM2940T-5.0 package="TO220 [THT]"]
  D15 = Schottky Diode [part_number=1N5818 package="300 mil [THT]"]
  C14 = Tantalum Capacitor [capacitance=47µF voltage=10V package="200 mil [THT, tantalum]"]
  C13 = Ceramic Capacitor [capacitance=0.1µF voltage=50V package="200 mil [THT, multilayer]"]
  C15 = Ceramic Capacitor [capacitance=0.1µF voltage=50V package="200 mil [THT, multilayer]"]
  C16 = Tantalum Capacitor [capacitance=10µF voltage=35V package="200 mil [THT, tantalum]"]
  U2 = V18ZA2P [part_number=ERZV14D220 package=v18za2p]
  R35 = Resistor [tolerance=±5% resistance=100k package=THT]
  R36 = Resistor [tolerance=±5% resistance=100k package=THT]
  R37 = Resistor [tolerance=±5% resistance=100k package=THT]
  R38 = Resistor [tolerance=±5% resistance=100k package=THT]
  IC3 = IC, DIP package, 8 pins [chip_label="Dual VR Conditioner"]
  JP1 = female pin header, 3 pins [form="♀ (female)"]
  JP2 = female pin header, 3 pins [form="♀ (female)"]
  JP3 = female pin header, 3 pins [form="♀ (female)"]
  R39 = Resistor [tolerance=±5% resistance=10k package=THT]
  JP4 = female pin header, 2 pins [form="♀ (female)"]
  R40 = Resistor [tolerance=±5% resistance=10k package=THT]
  JP5 = female pin header, 2 pins [form="♀ (female)"]
  C18 = Ceramic Capacitor [capacitance=0.3µF package="200 mil [THT, multilayer]"]
  R41 = Resistor [tolerance=±5% resistance=750 package=THT]
  MPX4250A = female pin header, 6 pins [form="♀ (female)"]
  C19 = Ceramic Capacitor [capacitance=0.01µF package="200 mil [THT, multilayer]"]
  C20 = Ceramic Capacitor [capacitance=1µF package="200 mil [THT, multilayer]"]
  R48 = Resistor [tolerance=±5% resistance=100k package=THT]
  R49 = Resistor [tolerance=±5% resistance=100k power=0.25W package=THT]
  R50 = Resistor [tolerance=±5% resistance=1k package=THT]
  R51 = Resistor [tolerance=±5% resistance=1k package=THT]
  R12 = Resistor [tolerance=±5% resistance=2.4k power=0.25W package=THT]
  D16 = Zener Diode [part_number=1N5919BG breakdown_voltage=5.1V package="300 mil [THT]"]
  R54 = Resistor [tolerance=±5% resistance=10k package=THT]
  D17 = Schottky Diode [part_number=1N5818 package="300 mil [THT]"]
  R55 = Resistor [tolerance=±5% resistance=100k package=THT]
  R56 = Resistor [tolerance=±5% resistance=100k power=0.25W package=THT]
  R57 = Resistor [tolerance=±5% resistance=1k package=THT]
  R58 = Resistor [tolerance=±5% resistance=1k package=THT]
  LED5 = LED - 3mm [color="Red (633nm)" package="3 mm [THT]"]
  LED6 = LED - 3mm [color="Red (633nm)" package="3 mm [THT]"]
  LED7 = LED - 3mm [color="Red (633nm)" package="3 mm [THT]"]
  LED8 = LED - 3mm [color="Red (633nm)" package="3 mm [THT]"]
  Q5 = Basic FET N-Channel [part_number=STP62NS04Z package="TO220 [THT]"]
  OLED1 = 128x32 I2C Monochrome OLED Display
  R32 = Resistor [tolerance=±5% resistance=160 power=2W package=THT]
  Q7 = Basic FET N-Channel [part_number=STP62NS04Z package="TO220 [THT]"]
  Q6 = Basic FET N-Channel [part_number=STP62NS04Z package="TO220 [THT]"]
  LED4 = LED - 3mm [color="Red (633nm)" package="3 mm [THT]"]
  LED3 = LED - 3mm [color="Red (633nm)" package="3 mm [THT]"]
  LED2 = LED - 3mm [color="Red (633nm)" package="3 mm [THT]"]
  LED1 = LED - 3mm [color="Red (633nm)" package="3 mm [THT]"]
  J4 = shrouded pin header, 40 pins [form="♂ (shrouded male)"]
  Q8 = Basic FET N-Channel [part_number=STP62NS04Z package="TO220 [THT]"]
  Pololu_A1 = Pololu A4988 [part_number=DRV8825 package=SO16]
  C23 = Ceramic Capacitor [capacitance=4.7nF package="200 mil [THT, multilayer]"]
  IC4 = ULN2803A [package=THT]
  J5 = COMPUTER-PERIPHERAL-POWER [package=computer-peripheral-power]  # not connected
  U3 = IC, SIP package, 12 pins [chip_label=IC]  # not connected

nets (from the schematic view):
  O2-CPU-A8: Arduino_Mega_2560.A8, R22.Pin_1, D13.cathode, C10.1, D14.anode
  IAT-CPU-A0: Arduino_Mega_2560.A0, R2.Pin_1, D1.anode, D2.cathode, C2.1
  CLT-CPU-A1: Arduino_Mega_2560.A1, R4.Pin_1, D3.anode, D4.cathode, C4.1
  TPS-CPU-A2: Arduino_Mega_2560.A2, R6.Pin_1, D5.anode, D6.cathode, C6.1
  MAP-CPU-A3: Arduino_Mega_2560.A3, C18.0, R41.Pin_1, J4.pin11
  BRV-CPU-A4: Arduino_Mega_2560.A4, R8.Pin_1, D8.cathode, D7.anode, C8.1
  SCL-CPU-D21: Arduino_Mega_2560.D21/SCL, Arduino_Mega_2560.SCL, OLED1.SCL
  TACH1-CPU-D19: Arduino_Mega_2560.D19/RX1, IC3.pin8, JP2.pin1
  TACH2-CPU-D18: Arduino_Mega_2560.D18/TX1, IC3.pin7, JP3.pin3
  STEP-CPU-D17: Arduino_Mega_2560.D17_PWM/RX2, Pololu_A1.STEP
  STEPDIR-CPU-D16: Arduino_Mega_2560.D16_PWM/TX2, Pololu_A1.DIR
  SDA-CPU-D20: Arduino_Mega_2560.SDA, OLED1.SDA
  GND: Arduino_Mega_2560.GND, D2.anode, D4.anode, D6.anode, D8.anode, Q1.source, R11.Pin_1, C7.0, C1.0, C3.0, C5.0, J3.pin1, Q2.source, R17.Pin_1, Q3.source, R14.Pin_1, Q4.source, R20.Pin_1, C2.0, C8.0, R21.Pin_1, C9.0, D13.anode, C6.0, C4.0, C10.0, IC1.pin3, C11.0, IC2.pin3, C12.0, U1.GND, C14.-, C13.0, C15.0, C16.-, U2.P$2, R35.Pin_0, R36.Pin_0, R37.Pin_0, R38.Pin_0, IC3.pin6, C18.1, MPX4250A.pin2, C19.0, C20.0, R48.Pin_0, R49.Pin_0, D16.anode, R55.Pin_0, R56.Pin_0, LED5.cathode, LED6.cathode, LED7.cathode, LED8.cathode, Q5.source, OLED1.GND, Q7.source, Q6.source, J4.pin9, J4.pin10, J4.pin12, J4.pin23, Q8.source, Pololu_A1.GND, C23.0, IC4.0V
  INJ4-CPU-D11: Arduino_Mega_2560.D11_PWM, R19.Pin_0, R20.Pin_0
  INJ3-CPU-D10: Arduino_Mega_2560.D10_PWM, R16.Pin_0, R17.Pin_0
  INJ2-CPU-D9: Arduino_Mega_2560.D9_PWM, R13.Pin_0, R14.Pin_0
  INJ1-CPU-D8: Arduino_Mega_2560.D8_PWM, R10.Pin_0, R11.Pin_0
  5V: Arduino_Mega_2560.IOREF, Arduino_Mega_2560.5V, R1.Pin_0, D1.cathode, R3.Pin_0, D3.cathode, D5.cathode, D7.cathode, D14.cathode, U1.output_voltage, C14.+, C13.1, IC3.pin5, JP1.pin1, R39.Pin_0, R40.Pin_0, MPX4250A.pin3, C19.1, C20.1, D16.cathode, R54.Pin_0, D17.cathode, OLED1.VIN, J4.pin13, J4.pin28, Pololu_A1.RESET, Pololu_A1.SLEEP, IC4.COM_-_Common
  RESET: Arduino_Mega_2560.RESET, R54.Pin_1, D17.anode, C23.1
  LS2-CPU-D5: Arduino_Mega_2560.D4_PWM, R58.Pin_0
  LS3-CPU-D6: Arduino_Mega_2560.D5_PWM, R50.Pin_0
  LS4-CPU-D4: Arduino_Mega_2560.D6_PWM, R57.Pin_0
  LS1-CPU-D7: Arduino_Mega_2560.D7_PWM, R51.Pin_0
  IGN2-CPU-D24: Arduino_Mega_2560.D38, R24.Pin_0
  IGN1-CPU-D28: Arduino_Mega_2560.D40, R23.Pin_0
  RST-CPU-D48: Arduino_Mega_2560.D43, OLED1.RST
  LC-CPU-D45: Arduino_Mega_2560.D45, IC4.In_4
  LC-CPU-D47: Arduino_Mega_2560.D47, IC4.In_5
  LC-CPU-D49: Arduino_Mega_2560.D49, IC4.In_6
  IGN4-CPU-D36: Arduino_Mega_2560.D50, R30.Pin_0
  LC-CPU-D51: Arduino_Mega_2560.D51, IC4.In_7
  IGN3-CPU-D40: Arduino_Mega_2560.D52, R29.Pin_0
  LC-CPU-D53: Arduino_Mega_2560.D53, IC4.In_8
  IAT Sensor: R1.Pin_1, R2.Pin_0, C1.1, J4.pin20
  CLT Sensor: R3.Pin_1, R4.Pin_0, C3.1, J4.pin19
  TPS Sensor: R6.Pin_0, C5.1, J4.pin22
  12V: R7.Pin_0, R9.Pin_0, R15.Pin_0, R18.Pin_0, U1.input_voltage, D15.cathode, C15.1, C16.+, JP1.pin3, R12.Pin_0, Pololu_A1.VMOT
  N1: R7.Pin_1, R8.Pin_0, C7.1, R21.Pin_0
  N2: R9.Pin_1, LED1.anode
  INJ-1-OUT: D9.cathode, Q1.drain, J4.pin1, J4.pin40
  N3: D9.anode, LED1.cathode
  N4: Q1.gate, R10.Pin_1
  12V-raw: J3.pin2, D15.anode, U2.P$1
  N5: R15.Pin_1, LED3.anode
  INJ-3-OUT: D11.cathode, Q2.drain, J4.pin3, J4.pin4
  N6: D11.anode, LED3.cathode
  N7: Q2.gate, R16.Pin_1
  INJ-2-OUT: D10.cathode, Q3.drain, J4.pin2, J4.pin39
  N8: D10.anode, LED2.cathode
  N9: Q3.gate, R13.Pin_1
  N10: R18.Pin_1, LED4.anode
  INJ-4-OUT: D12.cathode, Q4.drain, J4.pin5, J4.pin6
  N11: D12.anode, LED4.cathode
  N12: Q4.gate, R19.Pin_1
  O2 Sensor: C9.1, R22.Pin_0, J4.pin21
  N13: IC1.pin2, R23.Pin_1, R37.Pin_1
  N14: IC1.pin4, R24.Pin_1, R35.Pin_1
  N15: IC1.pin5, R25.Pin_0
  JP1-OUT: IC1.pin6, C11.1, IC2.pin6, C12.1, JP1.pin2
  N16: IC1.pin7, R27.Pin_1
  IGN-2-OUT: R25.Pin_1, R26.Pin_1, J4.pin34
  N17: R26.Pin_0, LED6.anode
  IGN-1-OUT: R27.Pin_0, R28.Pin_1, J4.pin7
  N18: R28.Pin_0, LED5.anode
  N19: IC2.pin2, R29.Pin_1, R38.Pin_1
  N20: IC2.pin4, R30.Pin_1, R36.Pin_1
  N21: IC2.pin5, R32.Pin_0
  N22: IC2.pin7, R31.Pin_1
  IGN-3-OUT: R31.Pin_0, R33.Pin_1, J4.pin33
  N23: R33.Pin_0, LED7.anode
  N24: R34.Pin_0, LED8.anode
  IGN-4-OUT: R34.Pin_1, R32.Pin_1, J4.pin8
  VR1-: IC3.pin1, J4.pin27
  N25: IC3.pin2, JP2.pin3
  N26: IC3.pin3, JP3.pin1
  VR2-: IC3.pin4, J4.pin26
  VR1+: JP2.pin2, JP4.pin2, J4.pin25
  VR2+: JP3.pin2, JP5.pin1, J4.pin24
  N27: R39.Pin_1, JP4.pin1
  N28: R40.Pin_1, JP5.pin2
  N29: R41.Pin_0, MPX4250A.pin1
  N30: R48.Pin_1, R50.Pin_1, Q7.gate
  N31: R49.Pin_1, R51.Pin_1, Q8.gate
  N32: R12.Pin_1, LED2.anode
  N33: R55.Pin_1, R57.Pin_1, Q5.gate
  N34: R56.Pin_1, R58.Pin_1, Q6.gate
  HC-1-OUT: Q5.drain, J4.pin36
  IDLE-OUT: Q7.drain, J4.pin37
  HC-2-OUT: Q6.drain, J4.pin38
  LC-1-OUT: J4.pin14, IC4.Out_4
  LC-2-OUT: J4.pin15, IC4.Out_5
  LC-3-OUT: J4.pin16, IC4.Out_6
  LC-4-OUT: J4.pin17, IC4.Out_7
  LC-5-OUT: J4.pin18, IC4.Out_8
  STEP-2B-OUT: J4.pin29, Pololu_A1.2B
  STEP-2A-OUT: J4.pin30, Pololu_A1.2A
  STEP-1A-OUT: J4.pin31, Pololu_A1.1A
  STEP-1B-OUT: J4.pin32, Pololu_A1.1B
  BOOST-OUT: J4.pin35, Q8.drain

notes:
  Inlet Air Temperature sensor
  Coolant Temperature Sensor
  Speeduino v0.4, Throttle Position Sensor
  Battery Reference Voltage
  Injector 1
  Speeduino v0.4, Connector 1
  Injector 3
  Injector 2
  Injector 4
  Speeduino v0.4, O2 Sensor
  Ignitor output 1
  Ignitor output 2
  12v
  5v
  Power supply
  IGN Out
  Crank and Cam sensors
  Speeduino v0.2, MAP sensor input
  Speeduino v0.4
  Generic Outputs - High Current
  inj1
  VR
  Hall
  Reset Protection - Refer AVR040 Application note
  128x32 OLED
  Stepper Driver
  PWM Idle / Boost
  TAPR 1.0
  © Josh Stewart
