# Fritzing sketch schematic v0.2 (saved by Fritzing 0.8.7b)
circuit board: 10cm x 13.8143cm
breadboards: 1

parts:
  Part1 = Arduino Mega 2560 (Rev3)
  R1 = Resistor [tolerance=±5% resistance=2.49k package=THT]
  R2 = Resistor [tolerance=±5% resistance=470 package=THT]
  D1 = Schottky Diode [part_number=1N5818 package="300 mil [THT]"]
  D2 = Schottky Diode [part_number=1N5818 package="300 mil [THT]"]
  C2 = Ceramic Capacitor [capacitance=0.22µF package="100 mil [THT, multilayer]"]
  R3 = Resistor [tolerance=±5% resistance=2.49k package=THT]
  C4 = Ceramic Capacitor [capacitance=0.22µF package="100 mil [THT, multilayer]"]
  R4 = Resistor [tolerance=±5% resistance=470 package=THT]
  D3 = Schottky Diode [part_number=1N5818 package="300 mil [THT]"]
  D4 = Schottky Diode [part_number=1N5818 package="300 mil [THT]"]
  J1 = screw terminal, 7 pins
  C6 = Ceramic Capacitor [capacitance=0.22µF package="100 mil [THT, multilayer]"]
  R6 = Resistor [tolerance=±5% resistance=470 package=THT]
  D5 = Schottky Diode [part_number=1N5818 package="300 mil [THT]"]
  D6 = Schottky Diode [part_number=1N5818 package="300 mil [THT]"]
  R7 = Resistor [tolerance=±5% resistance=3.9k package=THT]
  C8 = Ceramic Capacitor [capacitance=0.22µF package="100 mil [THT, multilayer]"]
  R8 = Resistor [tolerance=±5% resistance=470 package=THT]
  D8 = Schottky Diode [part_number=1N5818 package="300 mil [THT]"]
  D7 = Schottky Diode [part_number=1N5818 package="300 mil [THT]"]
  R9 = Resistor [tolerance=±5% resistance=2.2k package=THT]
  LED1 = LED - 5mm [color="Red (633nm)" package="5 mm [THT]"]
  D9 = Rectifier Diode [part_number=1N4004 package="300 mil [THT]"]
  Q1 = Basic FET N-Channel [part_number=VND7NV04 package="TO220 [THT]"]
  R10 = Resistor [tolerance=±5% resistance=1k package=THT]
  R11 = Resistor [tolerance=±5% resistance=100k package=THT]
  J2 = screw terminal, 4 pins
  C7 = Ceramic Capacitor [capacitance=0.1µF package="200 mil [THT, multilayer]"]
  C1 = Ceramic Capacitor [capacitance=0.1µF package="200 mil [THT, multilayer]"]
  C3 = Ceramic Capacitor [capacitance=0.1µF package="200 mil [THT, multilayer]"]
  C5 = Ceramic Capacitor [capacitance=0.1µF package="200 mil [THT, multilayer]"]
  J3 = screw terminal, 2 pins
  R12 = Resistor [tolerance=±5% resistance=2.2k package=THT]
  LED2 = LED - 5mm [color="Red (633nm)" package="5 mm [THT]"]
  D10 = Rectifier Diode [part_number=1N4004 package="300 mil [THT]"]
  Q2 = Basic FET N-Channel [part_number=VND7NV04 package="TO220 [THT]"]
  R13 = Resistor [tolerance=±5% resistance=1k package=THT]
  R14 = Resistor [tolerance=±5% resistance=100k package=THT]
  R15 = Resistor [tolerance=±5% resistance=2.2k package=THT]
  LED3 = LED - 5mm [color="Red (633nm)" package="5 mm [THT]"]
  D11 = Rectifier Diode [part_number=1N4004 package="300 mil [THT]"]
  Q3 = Basic FET N-Channel [part_number=VND7NV04 package="TO220 [THT]"]
  R16 = Resistor [tolerance=±5% resistance=1k package=THT]
  R17 = Resistor [tolerance=±5% resistance=100k package=THT]
  R18 = Resistor [tolerance=±5% resistance=2.2k package=THT]
  LED4 = LED - 5mm [color="Red (633nm)" package="5 mm [THT]"]
  D12 = Rectifier Diode [part_number=1N4004 package="300 mil [THT]"]
  Q4 = Basic FET N-Channel [part_number=VND7NV04 package="TO220 [THT]"]
  R19 = Resistor [tolerance=±5% resistance=1k package=THT]
  R20 = Resistor [tolerance=±5% resistance=100k package=THT]

nets:
  IAT-CPU-A0: Part1.A0, R2.Pin_1, D1.anode, D2.cathode, C2.1
  CLT-CPU-A1: Part1.A1, C4.1, R4.Pin_1, D3.anode, D4.cathode
  TPS-CPU-A2: Part1.A2, C6.1, R6.Pin_1, D5.anode, D6.cathode
  BRV-CPU-A3: Part1.A3, C8.1, R8.Pin_1, D8.cathode, D7.anode
  GND: Part1.GND, D2.anode, C2.0, C4.0, D4.anode, J1.pin1, C6.0, D6.anode, C8.0, D8.anode, Q1.source, R11.Pin_1, C7.0, C1.0, C3.0, C5.0, J3.pin1, Q2.source, R14.Pin_1, Q3.source, R17.Pin_1, Q4.source, R20.Pin_1
  INJ1-CPU-D8: Part1.D8_PWM, R10.Pin_0, R11.Pin_0, R19.Pin_0, R20.Pin_0
  5V: Part1.IOREF, Part1.5V, R1.Pin_0, D1.cathode, R3.Pin_0, D3.cathode, J1.pin2, J1.pin4, J1.pin6, D5.cathode, D7.cathode
  IAT Sensor: R1.Pin_1, R2.Pin_0, J1.pin7, C1.1
  CLT Sensor: R3.Pin_1, R4.Pin_0, J1.pin5, C3.1
  TPS Sensor: J1.pin3, R6.Pin_0, C5.1
  12v Input: R7.Pin_0
  N1: R7.Pin_1, R8.Pin_0, C7.1
  12V: R9.Pin_0, J3.pin2, R12.Pin_0, R15.Pin_0, R18.Pin_0
  N2: R9.Pin_1, LED1.anode
  N3: LED1.cathode, D9.anode
  INJ-1-OUT: D9.cathode, Q1.drain, J2.pin4
  N4: Q1.gate, R10.Pin_1
  N5: R12.Pin_1, LED2.anode
  N6: LED2.cathode, D10.anode
  INJ-3-OUT: D10.cathode, Q2.drain
  N7: Q2.gate, R13.Pin_1
  INJ3-CPU-D10: R13.Pin_0, R14.Pin_0
  N8: R15.Pin_1, LED3.anode
  N9: LED3.cathode, D11.anode
  INJ-2-OUT: D11.cathode, Q3.drain
  N10: Q3.gate, R16.Pin_1
  INJ2-CPU-D9: R16.Pin_0, R17.Pin_0
  N11: R18.Pin_1, LED4.anode
  N12: LED4.cathode, D12.anode
  INJ-4-OUT: D12.cathode, Q4.drain
  N13: Q4.gate, R19.Pin_1

notes:
  Inlet Air Temperature sensor
  Coolant Temperature Sensor
  Speeduino v0.2, Throttle Position Sensor
  Battery Reference Voltage
  Injector 1
  Sensor Screw connector 1
  Injector 3
  Injector 2
  Injector 4
