# Fritzing sketch schematic (saved by Fritzing 0.8.3b)
circuit board: 13cm x 5.74233cm
breadboards: 1

parts:
  R1 = Resistor [tolerance=±5% resistance=10k package=THT]
  U1 = Optocoupler [package=THT]
  D1 = Schottky Diode [part_number=1N5819 package="300 mil [THT]"]
  D2 = Schottky Diode [part_number=1N5819 package="300 mil [THT]"]
  R2 = Resistor [tolerance=±5% resistance=10k package=THT]
  Q1 = Basic FET N-Channel [part_number=STP62NS04Z package="TO220 [THT]"]
  Q2 = Basic FET N-Channel [part_number=STP62NS04Z package="TO220 [THT]"]
  R4 = Resistor [tolerance=±5% resistance=1k package=THT]
  R5 = Resistor [tolerance=±5% resistance=10k package=THT]
  R6 = Resistor [tolerance=±5% resistance=1k package=THT]
  Injector_Outputs = screw terminal, 2 pins
  Ignition_Outputs_1/2 = screw terminal, 2 pins
  C2 = Ceramic Capacitor [capacitance=100nF package="200 mil [THT, multilayer]"]
  C1 = Ceramic Capacitor [capacitance=100nF package="200 mil [THT, multilayer]"]
  R3 = Resistor [tolerance=±5% resistance=10k package=THT]
  Inputs = screw terminal, 7 pins
  12v_Input = screw terminal, 2 pins
  Arduino_Mega_2560 = Arduino Mega 2560 (Rev3)
  Injector_outputs_3/4 = screw terminal, 2 pins
  Ignition_outputs_3/4 = screw terminal, 2 pins
  Q3 = Basic FET N-Channel [part_number=STP62NS04Z package="TO220 [THT]"]
  Q4 = Basic FET N-Channel [part_number=NTD5867 package="TO220 [THT]"]
  D3 = Schottky Diode [part_number=1N5819 package="300 mil [THT]"]
  D4 = Schottky Diode [part_number=1N5819 package="300 mil [THT]"]
  C3 = Ceramic Capacitor [capacitance=100nF package="200 mil [THT, multilayer]"]
  C4 = Ceramic Capacitor [capacitance=100nF package="200 mil [THT, multilayer]"]
  R7 = Resistor [tolerance=±5% resistance=10k package=THT]
  R8 = Resistor [tolerance=±5% resistance=1k package=THT]
  R9 = Resistor [tolerance=±5% resistance=1k package=THT]
  R10 = Resistor [tolerance=±5% resistance=10k package=THT]
  J1 = female pin header, 3 pins [form="♀ (female)"]

nets:
  N1: R1.Pin_0, Inputs.pin2, Arduino_Mega_2560.5V, J1.pin1
  N2: R1.Pin_1, U1.Pin_5, Arduino_Mega_2560.D2_PWM
  N3: U1.Pin_1, R2.Pin_1, Inputs.pin1
  GND: U1.Pin_2, U1.Pin_4, Q1.source, Q2.source, R5.Pin_0, C2.0, C1.0, R3.Pin_1, 12v_Input.pin1, Arduino_Mega_2560.GND, Q3.source, Q4.source, C3.0, C4.0, R7.Pin_1, R10.Pin_0
  N4: D1.cathode, Ignition_Outputs_1/2.pin1, C1.1
  N5: D1.anode, Arduino_Mega_2560.D7_PWM
  N6: D2.cathode, Ignition_Outputs_1/2.pin2, C2.1
  N7: D2.anode, Arduino_Mega_2560.D6_PWM
  N8: R2.Pin_0, J1.pin2
  N9: Q1.gate, R4.Pin_0, R3.Pin_0
  N10: Q1.drain, Injector_Outputs.pin1
  N11: Q2.gate, R5.Pin_1, R6.Pin_1
  N12: Q2.drain, Injector_Outputs.pin2
  N13: R4.Pin_1, Arduino_Mega_2560.D9_PWM
  N14: R6.Pin_0, Arduino_Mega_2560.D8_PWM
  N15: Inputs.pin3, Arduino_Mega_2560.A0
  N16: Inputs.pin4, Arduino_Mega_2560.A1
  N17: Inputs.pin5, Arduino_Mega_2560.A2
  N18: Inputs.pin6, Arduino_Mega_2560.A3
  N19: Inputs.pin7, Arduino_Mega_2560.A4
  N20: 12v_Input.pin2, Arduino_Mega_2560.VIN, J1.pin3
  N21: Arduino_Mega_2560.D13_PWM, D3.anode
  N22: Arduino_Mega_2560.D12_PWM, D4.anode
  N23: Arduino_Mega_2560.D11_PWM, R9.Pin_0
  N24: Arduino_Mega_2560.D10_PWM, R8.Pin_1
  N25: Injector_outputs_3/4.pin1, Q3.drain
  N26: Injector_outputs_3/4.pin2, Q4.drain
  N27: Ignition_outputs_3/4.pin1, D4.cathode, C4.1
  N28: Ignition_outputs_3/4.pin2, D3.cathode, C3.1
  N29: Q3.gate, R9.Pin_1, R10.Pin_1
  N30: Q4.gate, R7.Pin_0, R8.Pin_0

notes:
  5V Sensor supply
  Crank
  TPS
  MAP
  +
  -
  Ign
  Inj
  3
  4
  5V
  IAT
  CLT
  Tach
  1
  2
  Kartduino
  O2
  v0.1
  By Josh Stewart
  12V
